// Logisim project AES.circ as structural Verilog: 19 circuits, main circuit test_aes
module aes (
  input  [31:0] m0,
  input  [31:0] m1,
  input  [31:0] m2,
  input  [31:0] m3,
  input  [31:0] k0,
  input  [31:0] k1,
  input  [31:0] k2,
  input  [31:0] k3,
  input  clk,
  output [31:0] c0,
  output [31:0] c1,
  output [31:0] c2,
  output [31:0] c3
);

  wire [7:0] first_turn_1_kout0, first_turn_1_kout1, first_turn_1_kout2, first_turn_1_kout3,
       first_turn_1_kout4, first_turn_1_kout4_2, first_turn_1_kout6, first_turn_1_kout7, first_turn_1_kout8,
       first_turn_1_kout9, first_turn_1_kout10, first_turn_1_kout11, first_turn_1_kout12,
       first_turn_1_kout13, first_turn_1_kout14, first_turn_1_kout15, first_turn_1_out0, first_turn_1_out1,
       first_turn_1_out2, first_turn_1_out3, first_turn_1_out4, first_turn_1_out5, first_turn_1_out6,
       first_turn_1_out7, first_turn_1_out8, first_turn_1_out9, first_turn_1_out10, first_turn_1_out11,
       first_turn_1_out12, first_turn_1_out13, first_turn_1_out14, first_turn_1_out15, one_turn_1_kout0,
       one_turn_1_kout1, one_turn_1_kout2, one_turn_1_kout3, one_turn_1_kout4, one_turn_1_kout4_2,
       one_turn_1_kout6, one_turn_1_kout7, one_turn_1_kout8, one_turn_1_kout9, one_turn_1_kout10,
       one_turn_1_kout11, one_turn_1_kout12, one_turn_1_kout13, one_turn_1_kout14, one_turn_1_kout15,
       one_turn_1_out0, one_turn_1_out1, one_turn_1_out2, one_turn_1_out3, one_turn_1_out4, one_turn_1_out5,
       one_turn_1_out6, one_turn_1_out7, one_turn_1_out8, one_turn_1_out9, one_turn_1_out10,
       one_turn_1_out11, one_turn_1_out12, one_turn_1_out13, one_turn_1_out14, one_turn_1_out15,
       one_turn_2_kout0, one_turn_2_kout1, one_turn_2_kout2, one_turn_2_kout3, one_turn_2_kout4,
       one_turn_2_kout4_2, one_turn_2_kout6, one_turn_2_kout7, one_turn_2_kout8, one_turn_2_kout9,
       one_turn_2_kout10, one_turn_2_kout11, one_turn_2_kout12, one_turn_2_kout13, one_turn_2_kout14,
       one_turn_2_kout15, one_turn_2_out0, one_turn_2_out1, one_turn_2_out2, one_turn_2_out3,
       one_turn_2_out4, one_turn_2_out5, one_turn_2_out6, one_turn_2_out7, one_turn_2_out8, one_turn_2_out9,
       one_turn_2_out10, one_turn_2_out11, one_turn_2_out12, one_turn_2_out13, one_turn_2_out14,
       one_turn_2_out15, one_turn_3_kout0, one_turn_3_kout1, one_turn_3_kout2, one_turn_3_kout3,
       one_turn_3_kout4, one_turn_3_kout4_2, one_turn_3_kout6, one_turn_3_kout7, one_turn_3_kout8,
       one_turn_3_kout9, one_turn_3_kout10, one_turn_3_kout11, one_turn_3_kout12, one_turn_3_kout13,
       one_turn_3_kout14, one_turn_3_kout15, one_turn_3_out0, one_turn_3_out1, one_turn_3_out2,
       one_turn_3_out3, one_turn_3_out4, one_turn_3_out5, one_turn_3_out6, one_turn_3_out7, one_turn_3_out8,
       one_turn_3_out9, one_turn_3_out10, one_turn_3_out11, one_turn_3_out12, one_turn_3_out13,
       one_turn_3_out14, one_turn_3_out15, one_turn_4_kout0, one_turn_4_kout1, one_turn_4_kout2,
       one_turn_4_kout3, one_turn_4_kout4, one_turn_4_kout4_2, one_turn_4_kout6, one_turn_4_kout7,
       one_turn_4_kout8, one_turn_4_kout9, one_turn_4_kout10, one_turn_4_kout11, one_turn_4_kout12,
       one_turn_4_kout13, one_turn_4_kout14, one_turn_4_kout15, one_turn_4_out0, one_turn_4_out1,
       one_turn_4_out2, one_turn_4_out3, one_turn_4_out4, one_turn_4_out5, one_turn_4_out6, one_turn_4_out7,
       one_turn_4_out8, one_turn_4_out9, one_turn_4_out10, one_turn_4_out11, one_turn_4_out12,
       one_turn_4_out13, one_turn_4_out14, one_turn_4_out15, one_turn_5_kout0, one_turn_5_kout1,
       one_turn_5_kout2, one_turn_5_kout3, one_turn_5_kout4, one_turn_5_kout4_2, one_turn_5_kout6,
       one_turn_5_kout7, one_turn_5_kout8, one_turn_5_kout9, one_turn_5_kout10, one_turn_5_kout11,
       one_turn_5_kout12, one_turn_5_kout13, one_turn_5_kout14, one_turn_5_kout15, one_turn_5_out0,
       one_turn_5_out1, one_turn_5_out2, one_turn_5_out3, one_turn_5_out4, one_turn_5_out5, one_turn_5_out6,
       one_turn_5_out7, one_turn_5_out8, one_turn_5_out9, one_turn_5_out10, one_turn_5_out11,
       one_turn_5_out12, one_turn_5_out13, one_turn_5_out14, one_turn_5_out15, one_turn_6_kout0,
       one_turn_6_kout1, one_turn_6_kout2, one_turn_6_kout3, one_turn_6_kout4, one_turn_6_kout4_2,
       one_turn_6_kout6, one_turn_6_kout7, one_turn_6_kout8, one_turn_6_kout9, one_turn_6_kout10,
       one_turn_6_kout11, one_turn_6_kout12, one_turn_6_kout13, one_turn_6_kout14, one_turn_6_kout15,
       one_turn_6_out0, one_turn_6_out1, one_turn_6_out2, one_turn_6_out3, one_turn_6_out4, one_turn_6_out5,
       one_turn_6_out6, one_turn_6_out7, one_turn_6_out8, one_turn_6_out9, one_turn_6_out10,
       one_turn_6_out11, one_turn_6_out12, one_turn_6_out13, one_turn_6_out14, one_turn_6_out15,
       one_turn_7_kout0, one_turn_7_kout1, one_turn_7_kout2, one_turn_7_kout3, one_turn_7_kout4,
       one_turn_7_kout4_2, one_turn_7_kout6, one_turn_7_kout7, one_turn_7_kout8, one_turn_7_kout9,
       one_turn_7_kout10, one_turn_7_kout11, one_turn_7_kout12, one_turn_7_kout13, one_turn_7_kout14,
       one_turn_7_kout15, one_turn_7_out0, one_turn_7_out1, one_turn_7_out2, one_turn_7_out3,
       one_turn_7_out4, one_turn_7_out5, one_turn_7_out6, one_turn_7_out7, one_turn_7_out8, one_turn_7_out9,
       one_turn_7_out10, one_turn_7_out11, one_turn_7_out12, one_turn_7_out13, one_turn_7_out14,
       one_turn_7_out15, one_turn_8_kout0, one_turn_8_kout1, one_turn_8_kout2, one_turn_8_kout3,
       one_turn_8_kout4, one_turn_8_kout4_2, one_turn_8_kout6, one_turn_8_kout7, one_turn_8_kout8,
       one_turn_8_kout9, one_turn_8_kout10, one_turn_8_kout11, one_turn_8_kout12, one_turn_8_kout13,
       one_turn_8_kout14, one_turn_8_kout15, one_turn_8_out0, one_turn_8_out1, one_turn_8_out2,
       one_turn_8_out3, one_turn_8_out4, one_turn_8_out5, one_turn_8_out6, one_turn_8_out7, one_turn_8_out8,
       one_turn_8_out9, one_turn_8_out10, one_turn_8_out11, one_turn_8_out12, one_turn_8_out13,
       one_turn_8_out14, one_turn_8_out15, one_turn_9_kout0, one_turn_9_kout1, one_turn_9_kout2,
       one_turn_9_kout3, one_turn_9_kout4, one_turn_9_kout4_2, one_turn_9_kout6, one_turn_9_kout7,
       one_turn_9_kout8, one_turn_9_kout9, one_turn_9_kout10, one_turn_9_kout11, one_turn_9_kout12,
       one_turn_9_kout13, one_turn_9_kout14, one_turn_9_kout15, one_turn_9_out0, one_turn_9_out1,
       one_turn_9_out2, one_turn_9_out3, one_turn_9_out4, one_turn_9_out5, one_turn_9_out6, one_turn_9_out7,
       one_turn_9_out8, one_turn_9_out9, one_turn_9_out10, one_turn_9_out11, one_turn_9_out12,
       one_turn_9_out13, one_turn_9_out14, one_turn_9_out15, register256_1_kout0, register256_1_kout1,
       register256_1_kout2, register256_1_kout3, register256_1_kout4, register256_1_kout5,
       register256_1_kout6, register256_1_kout7, register256_1_kout8, register256_1_kout9,
       register256_1_kout10, register256_1_kout11, register256_1_kout12, register256_1_kout13,
       register256_1_kout14, register256_1_kout15, register256_1_out0, register256_1_out1,
       register256_1_out2, register256_1_out3, register256_1_out4, register256_1_out5, register256_1_out6,
       register256_1_out7, register256_1_out8, register256_1_out9, register256_1_out10, register256_1_out11,
       register256_1_out12, register256_1_out13, register256_1_out14, register256_1_out15,
       register256_2_kout0, register256_2_kout1, register256_2_kout2, register256_2_kout3,
       register256_2_kout4, register256_2_kout5, register256_2_kout6, register256_2_kout7,
       register256_2_kout8, register256_2_kout9, register256_2_kout10, register256_2_kout11,
       register256_2_kout12, register256_2_kout13, register256_2_kout14, register256_2_kout15,
       register256_2_out0, register256_2_out1, register256_2_out2, register256_2_out3, register256_2_out4,
       register256_2_out5, register256_2_out6, register256_2_out7, register256_2_out8, register256_2_out9,
       register256_2_out10, register256_2_out11, register256_2_out12, register256_2_out13,
       register256_2_out14, register256_2_out15, register256_3_kout0, register256_3_kout1,
       register256_3_kout2, register256_3_kout3, register256_3_kout4, register256_3_kout5,
       register256_3_kout6, register256_3_kout7, register256_3_kout8, register256_3_kout9,
       register256_3_kout10, register256_3_kout11, register256_3_kout12, register256_3_kout13,
       register256_3_kout14, register256_3_kout15, register256_3_out0, register256_3_out1,
       register256_3_out2, register256_3_out3, register256_3_out4, register256_3_out5, register256_3_out6,
       register256_3_out7, register256_3_out8, register256_3_out9, register256_3_out10, register256_3_out11,
       register256_3_out12, register256_3_out13, register256_3_out14, register256_3_out15,
       register256_4_kout0, register256_4_kout1, register256_4_kout2, register256_4_kout3,
       register256_4_kout4, register256_4_kout5, register256_4_kout6, register256_4_kout7,
       register256_4_kout8, register256_4_kout9, register256_4_kout10, register256_4_kout11,
       register256_4_kout12, register256_4_kout13, register256_4_kout14, register256_4_kout15,
       register256_4_out0, register256_4_out1, register256_4_out2, register256_4_out3, register256_4_out4,
       register256_4_out5, register256_4_out6, register256_4_out7, register256_4_out8, register256_4_out9,
       register256_4_out10, register256_4_out11, register256_4_out12, register256_4_out13,
       register256_4_out14, register256_4_out15, register256_5_kout0, register256_5_kout1,
       register256_5_kout2, register256_5_kout3, register256_5_kout4, register256_5_kout5,
       register256_5_kout6, register256_5_kout7, register256_5_kout8, register256_5_kout9,
       register256_5_kout10, register256_5_kout11, register256_5_kout12, register256_5_kout13,
       register256_5_kout14, register256_5_kout15, register256_5_out0, register256_5_out1,
       register256_5_out2, register256_5_out3, register256_5_out4, register256_5_out5, register256_5_out6,
       register256_5_out7, register256_5_out8, register256_5_out9, register256_5_out10, register256_5_out11,
       register256_5_out12, register256_5_out13, register256_5_out14, register256_5_out15,
       register256_6_kout0, register256_6_kout1, register256_6_kout2, register256_6_kout3,
       register256_6_kout4, register256_6_kout5, register256_6_kout6, register256_6_kout7,
       register256_6_kout8, register256_6_kout9, register256_6_kout10, register256_6_kout11,
       register256_6_kout12, register256_6_kout13, register256_6_kout14, register256_6_kout15,
       register256_6_out0, register256_6_out1, register256_6_out2, register256_6_out3, register256_6_out4,
       register256_6_out5, register256_6_out6, register256_6_out7, register256_6_out8, register256_6_out9,
       register256_6_out10, register256_6_out11, register256_6_out12, register256_6_out13,
       register256_6_out14, register256_6_out15, register256_7_kout0, register256_7_kout1,
       register256_7_kout2, register256_7_kout3, register256_7_kout4, register256_7_kout5,
       register256_7_kout6, register256_7_kout7, register256_7_kout8, register256_7_kout9,
       register256_7_kout10, register256_7_kout11, register256_7_kout12, register256_7_kout13,
       register256_7_kout14, register256_7_kout15, register256_7_out0, register256_7_out1,
       register256_7_out2, register256_7_out3, register256_7_out4, register256_7_out5, register256_7_out6,
       register256_7_out7, register256_7_out8, register256_7_out9, register256_7_out10, register256_7_out11,
       register256_7_out12, register256_7_out13, register256_7_out14, register256_7_out15,
       register256_8_kout0, register256_8_kout1, register256_8_kout2, register256_8_kout3,
       register256_8_kout4, register256_8_kout5, register256_8_kout6, register256_8_kout7,
       register256_8_kout8, register256_8_kout9, register256_8_kout10, register256_8_kout11,
       register256_8_kout12, register256_8_kout13, register256_8_kout14, register256_8_kout15,
       register256_8_out0, register256_8_out1, register256_8_out2, register256_8_out3, register256_8_out4,
       register256_8_out5, register256_8_out6, register256_8_out7, register256_8_out8, register256_8_out9,
       register256_8_out10, register256_8_out11, register256_8_out12, register256_8_out13,
       register256_8_out14, register256_8_out15, register256_9_kout0, register256_9_kout1,
       register256_9_kout2, register256_9_kout3, register256_9_kout4, register256_9_kout5,
       register256_9_kout6, register256_9_kout7, register256_9_kout8, register256_9_kout9,
       register256_9_kout10, register256_9_kout11, register256_9_kout12, register256_9_kout13,
       register256_9_kout14, register256_9_kout15, register256_9_out0, register256_9_out1,
       register256_9_out2, register256_9_out3, register256_9_out4, register256_9_out5, register256_9_out6,
       register256_9_out7, register256_9_out8, register256_9_out9, register256_9_out10, register256_9_out11,
       register256_9_out12, register256_9_out13, register256_9_out14, register256_9_out15,
       register256_10_kout0, register256_10_kout1, register256_10_kout2, register256_10_kout3,
       register256_10_kout4, register256_10_kout5, register256_10_kout6, register256_10_kout7,
       register256_10_kout8, register256_10_kout9, register256_10_kout10, register256_10_kout11,
       register256_10_kout12, register256_10_kout13, register256_10_kout14, register256_10_kout15,
       register256_10_out0, register256_10_out1, register256_10_out2, register256_10_out3,
       register256_10_out4, register256_10_out5, register256_10_out6, register256_10_out7,
       register256_10_out8, register256_10_out9, register256_10_out10, register256_10_out11,
       register256_10_out12, register256_10_out13, register256_10_out14, register256_10_out15;

  first_turn first_turn_1 (
    .in0(m0[31:24]), .in1(m0[23:16]), .in2(m0[15:8]), .in3(m0[7:0]), .in4(m1[31:24]), .in5(m1[23:16]),
    .in6(m1[15:8]), .in7(m1[7:0]), .in8(m2[31:24]), .in9(m2[23:16]), .in10(m2[15:8]), .in11(m2[7:0]),
    .in12(m3[31:24]), .in13(m3[23:16]), .in14(m3[15:8]), .in15(m3[7:0]), .kin0(k0[31:24]), .kin1(k0[23:16]),
    .kin2(k0[15:8]), .kin3(k0[7:0]), .kin4(k1[31:24]), .kin4_2(k1[23:16]), .kin6(k1[15:8]), .kin7(k1[7:0]),
    .kin8(k2[31:24]), .kin9(k2[23:16]), .kin10(k2[15:8]), .kin11(k2[7:0]), .kin12(k3[31:24]),
    .kin13(k3[23:16]), .kin14(k3[15:8]), .kin15(k3[7:0]), .out0(first_turn_1_out0), .out1(first_turn_1_out1),
    .out2(first_turn_1_out2), .out3(first_turn_1_out3), .out4(first_turn_1_out4), .out5(first_turn_1_out5),
    .out6(first_turn_1_out6), .out7(first_turn_1_out7), .out8(first_turn_1_out8), .out9(first_turn_1_out9),
    .out10(first_turn_1_out10), .out11(first_turn_1_out11), .out12(first_turn_1_out12),
    .out13(first_turn_1_out13), .out14(first_turn_1_out14), .out15(first_turn_1_out15),
    .kout0(first_turn_1_kout0), .kout1(first_turn_1_kout1), .kout2(first_turn_1_kout2),
    .kout3(first_turn_1_kout3), .kout4(first_turn_1_kout4), .kout4_2(first_turn_1_kout4_2),
    .kout6(first_turn_1_kout6), .kout7(first_turn_1_kout7), .kout8(first_turn_1_kout8),
    .kout9(first_turn_1_kout9), .kout10(first_turn_1_kout10), .kout11(first_turn_1_kout11),
    .kout12(first_turn_1_kout12), .kout13(first_turn_1_kout13), .kout14(first_turn_1_kout14),
    .kout15(first_turn_1_kout15));
  register256 register256_1 (
    .in0(first_turn_1_out0), .in8(first_turn_1_out8), .in1(first_turn_1_out1), .in9(first_turn_1_out9),
    .in2(first_turn_1_out2), .in10(first_turn_1_out10), .in3(first_turn_1_out3), .in11(first_turn_1_out11),
    .in4(first_turn_1_out4), .in12(first_turn_1_out12), .in5(first_turn_1_out5), .in13(first_turn_1_out13),
    .in6(first_turn_1_out6), .in14(first_turn_1_out14), .in7(first_turn_1_out7), .in15(first_turn_1_out15),
    .kin0(first_turn_1_kout0), .kin8(first_turn_1_kout8), .kin1(first_turn_1_kout1),
    .kin9(first_turn_1_kout9), .kin2(first_turn_1_kout2), .kin10(first_turn_1_kout10),
    .kin3(first_turn_1_kout3), .kin11(first_turn_1_kout11), .kin4(first_turn_1_kout4),
    .kin12(first_turn_1_kout12), .kin5(first_turn_1_kout4_2), .kin13(first_turn_1_kout13),
    .kin6(first_turn_1_kout6), .kin14(first_turn_1_kout14), .kin7(first_turn_1_kout7),
    .kin15(first_turn_1_kout15), .clk(clk), .out0(register256_1_out0), .out8(register256_1_out8),
    .out1(register256_1_out1), .out9(register256_1_out9), .out2(register256_1_out2),
    .out10(register256_1_out10), .out3(register256_1_out3), .out11(register256_1_out11),
    .out4(register256_1_out4), .out12(register256_1_out12), .out5(register256_1_out5),
    .out13(register256_1_out13), .out6(register256_1_out6), .out14(register256_1_out14),
    .out7(register256_1_out7), .out15(register256_1_out15), .kout0(register256_1_kout0),
    .kout8(register256_1_kout8), .kout1(register256_1_kout1), .kout9(register256_1_kout9),
    .kout2(register256_1_kout2), .kout10(register256_1_kout10), .kout3(register256_1_kout3),
    .kout11(register256_1_kout11), .kout4(register256_1_kout4), .kout12(register256_1_kout12),
    .kout5(register256_1_kout5), .kout13(register256_1_kout13), .kout6(register256_1_kout6),
    .kout14(register256_1_kout14), .kout7(register256_1_kout7), .kout15(register256_1_kout15));
  one_turn one_turn_1 (
    .in0(register256_1_out0), .in1(register256_1_out1), .in2(register256_1_out2), .in3(register256_1_out3),
    .in4(register256_1_out4), .in5(register256_1_out5), .in6(register256_1_out6), .in7(register256_1_out7),
    .in8(register256_1_out8), .in9(register256_1_out9), .in10(register256_1_out10),
    .in11(register256_1_out11), .in12(register256_1_out12), .in13(register256_1_out13),
    .in14(register256_1_out14), .in15(register256_1_out15), .kin0(register256_1_kout0),
    .kin1(register256_1_kout1), .kin2(register256_1_kout2), .kin3(register256_1_kout3),
    .kin4(register256_1_kout4), .kin4_2(register256_1_kout5), .kin6(register256_1_kout6),
    .kin7(register256_1_kout7), .kin8(register256_1_kout8), .kin9(register256_1_kout9),
    .kin10(register256_1_kout10), .kin11(register256_1_kout11), .kin12(register256_1_kout12),
    .kin13(register256_1_kout13), .kin14(register256_1_kout14), .kin15(register256_1_kout15),
    .turn_number(4'b0001), .out0(one_turn_1_out0), .out1(one_turn_1_out1), .out2(one_turn_1_out2),
    .out3(one_turn_1_out3), .out4(one_turn_1_out4), .out5(one_turn_1_out5), .out6(one_turn_1_out6),
    .out7(one_turn_1_out7), .out8(one_turn_1_out8), .out9(one_turn_1_out9), .out10(one_turn_1_out10),
    .out11(one_turn_1_out11), .out12(one_turn_1_out12), .out13(one_turn_1_out13), .out14(one_turn_1_out14),
    .out15(one_turn_1_out15), .kout0(one_turn_1_kout0), .kout1(one_turn_1_kout1), .kout2(one_turn_1_kout2),
    .kout3(one_turn_1_kout3), .kout4(one_turn_1_kout4), .kout4_2(one_turn_1_kout4_2),
    .kout6(one_turn_1_kout6), .kout7(one_turn_1_kout7), .kout8(one_turn_1_kout8), .kout9(one_turn_1_kout9),
    .kout10(one_turn_1_kout10), .kout11(one_turn_1_kout11), .kout12(one_turn_1_kout12),
    .kout13(one_turn_1_kout13), .kout14(one_turn_1_kout14), .kout15(one_turn_1_kout15));
  register256 register256_2 (
    .in0(one_turn_1_out0), .in8(one_turn_1_out8), .in1(one_turn_1_out1), .in9(one_turn_1_out9),
    .in2(one_turn_1_out2), .in10(one_turn_1_out10), .in3(one_turn_1_out3), .in11(one_turn_1_out11),
    .in4(one_turn_1_out4), .in12(one_turn_1_out12), .in5(one_turn_1_out5), .in13(one_turn_1_out13),
    .in6(one_turn_1_out6), .in14(one_turn_1_out14), .in7(one_turn_1_out7), .in15(one_turn_1_out15),
    .kin0(one_turn_1_kout0), .kin8(one_turn_1_kout8), .kin1(one_turn_1_kout1), .kin9(one_turn_1_kout9),
    .kin2(one_turn_1_kout2), .kin10(one_turn_1_kout10), .kin3(one_turn_1_kout3), .kin11(one_turn_1_kout11),
    .kin4(one_turn_1_kout4), .kin12(one_turn_1_kout12), .kin5(one_turn_1_kout4_2), .kin13(one_turn_1_kout13),
    .kin6(one_turn_1_kout6), .kin14(one_turn_1_kout14), .kin7(one_turn_1_kout7), .kin15(one_turn_1_kout15),
    .clk(clk), .out0(register256_2_out0), .out8(register256_2_out8), .out1(register256_2_out1),
    .out9(register256_2_out9), .out2(register256_2_out2), .out10(register256_2_out10),
    .out3(register256_2_out3), .out11(register256_2_out11), .out4(register256_2_out4),
    .out12(register256_2_out12), .out5(register256_2_out5), .out13(register256_2_out13),
    .out6(register256_2_out6), .out14(register256_2_out14), .out7(register256_2_out7),
    .out15(register256_2_out15), .kout0(register256_2_kout0), .kout8(register256_2_kout8),
    .kout1(register256_2_kout1), .kout9(register256_2_kout9), .kout2(register256_2_kout2),
    .kout10(register256_2_kout10), .kout3(register256_2_kout3), .kout11(register256_2_kout11),
    .kout4(register256_2_kout4), .kout12(register256_2_kout12), .kout5(register256_2_kout5),
    .kout13(register256_2_kout13), .kout6(register256_2_kout6), .kout14(register256_2_kout14),
    .kout7(register256_2_kout7), .kout15(register256_2_kout15));
  one_turn one_turn_2 (
    .in0(register256_2_out0), .in1(register256_2_out1), .in2(register256_2_out2), .in3(register256_2_out3),
    .in4(register256_2_out4), .in5(register256_2_out5), .in6(register256_2_out6), .in7(register256_2_out7),
    .in8(register256_2_out8), .in9(register256_2_out9), .in10(register256_2_out10),
    .in11(register256_2_out11), .in12(register256_2_out12), .in13(register256_2_out13),
    .in14(register256_2_out14), .in15(register256_2_out15), .kin0(register256_2_kout0),
    .kin1(register256_2_kout1), .kin2(register256_2_kout2), .kin3(register256_2_kout3),
    .kin4(register256_2_kout4), .kin4_2(register256_2_kout5), .kin6(register256_2_kout6),
    .kin7(register256_2_kout7), .kin8(register256_2_kout8), .kin9(register256_2_kout9),
    .kin10(register256_2_kout10), .kin11(register256_2_kout11), .kin12(register256_2_kout12),
    .kin13(register256_2_kout13), .kin14(register256_2_kout14), .kin15(register256_2_kout15),
    .turn_number(4'b0010), .out0(one_turn_2_out0), .out1(one_turn_2_out1), .out2(one_turn_2_out2),
    .out3(one_turn_2_out3), .out4(one_turn_2_out4), .out5(one_turn_2_out5), .out6(one_turn_2_out6),
    .out7(one_turn_2_out7), .out8(one_turn_2_out8), .out9(one_turn_2_out9), .out10(one_turn_2_out10),
    .out11(one_turn_2_out11), .out12(one_turn_2_out12), .out13(one_turn_2_out13), .out14(one_turn_2_out14),
    .out15(one_turn_2_out15), .kout0(one_turn_2_kout0), .kout1(one_turn_2_kout1), .kout2(one_turn_2_kout2),
    .kout3(one_turn_2_kout3), .kout4(one_turn_2_kout4), .kout4_2(one_turn_2_kout4_2),
    .kout6(one_turn_2_kout6), .kout7(one_turn_2_kout7), .kout8(one_turn_2_kout8), .kout9(one_turn_2_kout9),
    .kout10(one_turn_2_kout10), .kout11(one_turn_2_kout11), .kout12(one_turn_2_kout12),
    .kout13(one_turn_2_kout13), .kout14(one_turn_2_kout14), .kout15(one_turn_2_kout15));
  register256 register256_3 (
    .in0(one_turn_2_out0), .in8(one_turn_2_out8), .in1(one_turn_2_out1), .in9(one_turn_2_out9),
    .in2(one_turn_2_out2), .in10(one_turn_2_out10), .in3(one_turn_2_out3), .in11(one_turn_2_out11),
    .in4(one_turn_2_out4), .in12(one_turn_2_out12), .in5(one_turn_2_out5), .in13(one_turn_2_out13),
    .in6(one_turn_2_out6), .in14(one_turn_2_out14), .in7(one_turn_2_out7), .in15(one_turn_2_out15),
    .kin0(one_turn_2_kout0), .kin8(one_turn_2_kout8), .kin1(one_turn_2_kout1), .kin9(one_turn_2_kout9),
    .kin2(one_turn_2_kout2), .kin10(one_turn_2_kout10), .kin3(one_turn_2_kout3), .kin11(one_turn_2_kout11),
    .kin4(one_turn_2_kout4), .kin12(one_turn_2_kout12), .kin5(one_turn_2_kout4_2), .kin13(one_turn_2_kout13),
    .kin6(one_turn_2_kout6), .kin14(one_turn_2_kout14), .kin7(one_turn_2_kout7), .kin15(one_turn_2_kout15),
    .clk(clk), .out0(register256_3_out0), .out8(register256_3_out8), .out1(register256_3_out1),
    .out9(register256_3_out9), .out2(register256_3_out2), .out10(register256_3_out10),
    .out3(register256_3_out3), .out11(register256_3_out11), .out4(register256_3_out4),
    .out12(register256_3_out12), .out5(register256_3_out5), .out13(register256_3_out13),
    .out6(register256_3_out6), .out14(register256_3_out14), .out7(register256_3_out7),
    .out15(register256_3_out15), .kout0(register256_3_kout0), .kout8(register256_3_kout8),
    .kout1(register256_3_kout1), .kout9(register256_3_kout9), .kout2(register256_3_kout2),
    .kout10(register256_3_kout10), .kout3(register256_3_kout3), .kout11(register256_3_kout11),
    .kout4(register256_3_kout4), .kout12(register256_3_kout12), .kout5(register256_3_kout5),
    .kout13(register256_3_kout13), .kout6(register256_3_kout6), .kout14(register256_3_kout14),
    .kout7(register256_3_kout7), .kout15(register256_3_kout15));
  one_turn one_turn_3 (
    .in0(register256_3_out0), .in1(register256_3_out1), .in2(register256_3_out2), .in3(register256_3_out3),
    .in4(register256_3_out4), .in5(register256_3_out5), .in6(register256_3_out6), .in7(register256_3_out7),
    .in8(register256_3_out8), .in9(register256_3_out9), .in10(register256_3_out10),
    .in11(register256_3_out11), .in12(register256_3_out12), .in13(register256_3_out13),
    .in14(register256_3_out14), .in15(register256_3_out15), .kin0(register256_3_kout0),
    .kin1(register256_3_kout1), .kin2(register256_3_kout2), .kin3(register256_3_kout3),
    .kin4(register256_3_kout4), .kin4_2(register256_3_kout5), .kin6(register256_3_kout6),
    .kin7(register256_3_kout7), .kin8(register256_3_kout8), .kin9(register256_3_kout9),
    .kin10(register256_3_kout10), .kin11(register256_3_kout11), .kin12(register256_3_kout12),
    .kin13(register256_3_kout13), .kin14(register256_3_kout14), .kin15(register256_3_kout15),
    .turn_number(4'b0011), .out0(one_turn_3_out0), .out1(one_turn_3_out1), .out2(one_turn_3_out2),
    .out3(one_turn_3_out3), .out4(one_turn_3_out4), .out5(one_turn_3_out5), .out6(one_turn_3_out6),
    .out7(one_turn_3_out7), .out8(one_turn_3_out8), .out9(one_turn_3_out9), .out10(one_turn_3_out10),
    .out11(one_turn_3_out11), .out12(one_turn_3_out12), .out13(one_turn_3_out13), .out14(one_turn_3_out14),
    .out15(one_turn_3_out15), .kout0(one_turn_3_kout0), .kout1(one_turn_3_kout1), .kout2(one_turn_3_kout2),
    .kout3(one_turn_3_kout3), .kout4(one_turn_3_kout4), .kout4_2(one_turn_3_kout4_2),
    .kout6(one_turn_3_kout6), .kout7(one_turn_3_kout7), .kout8(one_turn_3_kout8), .kout9(one_turn_3_kout9),
    .kout10(one_turn_3_kout10), .kout11(one_turn_3_kout11), .kout12(one_turn_3_kout12),
    .kout13(one_turn_3_kout13), .kout14(one_turn_3_kout14), .kout15(one_turn_3_kout15));
  register256 register256_4 (
    .in0(one_turn_3_out0), .in8(one_turn_3_out8), .in1(one_turn_3_out1), .in9(one_turn_3_out9),
    .in2(one_turn_3_out2), .in10(one_turn_3_out10), .in3(one_turn_3_out3), .in11(one_turn_3_out11),
    .in4(one_turn_3_out4), .in12(one_turn_3_out12), .in5(one_turn_3_out5), .in13(one_turn_3_out13),
    .in6(one_turn_3_out6), .in14(one_turn_3_out14), .in7(one_turn_3_out7), .in15(one_turn_3_out15),
    .kin0(one_turn_3_kout0), .kin8(one_turn_3_kout8), .kin1(one_turn_3_kout1), .kin9(one_turn_3_kout9),
    .kin2(one_turn_3_kout2), .kin10(one_turn_3_kout10), .kin3(one_turn_3_kout3), .kin11(one_turn_3_kout11),
    .kin4(one_turn_3_kout4), .kin12(one_turn_3_kout12), .kin5(one_turn_3_kout4_2), .kin13(one_turn_3_kout13),
    .kin6(one_turn_3_kout6), .kin14(one_turn_3_kout14), .kin7(one_turn_3_kout7), .kin15(one_turn_3_kout15),
    .clk(clk), .out0(register256_4_out0), .out8(register256_4_out8), .out1(register256_4_out1),
    .out9(register256_4_out9), .out2(register256_4_out2), .out10(register256_4_out10),
    .out3(register256_4_out3), .out11(register256_4_out11), .out4(register256_4_out4),
    .out12(register256_4_out12), .out5(register256_4_out5), .out13(register256_4_out13),
    .out6(register256_4_out6), .out14(register256_4_out14), .out7(register256_4_out7),
    .out15(register256_4_out15), .kout0(register256_4_kout0), .kout8(register256_4_kout8),
    .kout1(register256_4_kout1), .kout9(register256_4_kout9), .kout2(register256_4_kout2),
    .kout10(register256_4_kout10), .kout3(register256_4_kout3), .kout11(register256_4_kout11),
    .kout4(register256_4_kout4), .kout12(register256_4_kout12), .kout5(register256_4_kout5),
    .kout13(register256_4_kout13), .kout6(register256_4_kout6), .kout14(register256_4_kout14),
    .kout7(register256_4_kout7), .kout15(register256_4_kout15));
  register256 register256_5 (
    .in0(one_turn_4_out0), .in8(one_turn_4_out8), .in1(one_turn_4_out1), .in9(one_turn_4_out9),
    .in2(one_turn_4_out2), .in10(one_turn_4_out10), .in3(one_turn_4_out3), .in11(one_turn_4_out11),
    .in4(one_turn_4_out4), .in12(one_turn_4_out12), .in5(one_turn_4_out5), .in13(one_turn_4_out13),
    .in6(one_turn_4_out6), .in14(one_turn_4_out14), .in7(one_turn_4_out7), .in15(one_turn_4_out15),
    .kin0(one_turn_4_kout0), .kin8(one_turn_4_kout8), .kin1(one_turn_4_kout1), .kin9(one_turn_4_kout9),
    .kin2(one_turn_4_kout2), .kin10(one_turn_4_kout10), .kin3(one_turn_4_kout3), .kin11(one_turn_4_kout11),
    .kin4(one_turn_4_kout4), .kin12(one_turn_4_kout12), .kin5(one_turn_4_kout4_2), .kin13(one_turn_4_kout13),
    .kin6(one_turn_4_kout6), .kin14(one_turn_4_kout14), .kin7(one_turn_4_kout7), .kin15(one_turn_4_kout15),
    .clk(clk), .out0(register256_5_out0), .out8(register256_5_out8), .out1(register256_5_out1),
    .out9(register256_5_out9), .out2(register256_5_out2), .out10(register256_5_out10),
    .out3(register256_5_out3), .out11(register256_5_out11), .out4(register256_5_out4),
    .out12(register256_5_out12), .out5(register256_5_out5), .out13(register256_5_out13),
    .out6(register256_5_out6), .out14(register256_5_out14), .out7(register256_5_out7),
    .out15(register256_5_out15), .kout0(register256_5_kout0), .kout8(register256_5_kout8),
    .kout1(register256_5_kout1), .kout9(register256_5_kout9), .kout2(register256_5_kout2),
    .kout10(register256_5_kout10), .kout3(register256_5_kout3), .kout11(register256_5_kout11),
    .kout4(register256_5_kout4), .kout12(register256_5_kout12), .kout5(register256_5_kout5),
    .kout13(register256_5_kout13), .kout6(register256_5_kout6), .kout14(register256_5_kout14),
    .kout7(register256_5_kout7), .kout15(register256_5_kout15));
  one_turn one_turn_4 (
    .in0(register256_4_out0), .in1(register256_4_out1), .in2(register256_4_out2), .in3(register256_4_out3),
    .in4(register256_4_out4), .in5(register256_4_out5), .in6(register256_4_out6), .in7(register256_4_out7),
    .in8(register256_4_out8), .in9(register256_4_out9), .in10(register256_4_out10),
    .in11(register256_4_out11), .in12(register256_4_out12), .in13(register256_4_out13),
    .in14(register256_4_out14), .in15(register256_4_out15), .kin0(register256_4_kout0),
    .kin1(register256_4_kout1), .kin2(register256_4_kout2), .kin3(register256_4_kout3),
    .kin4(register256_4_kout4), .kin4_2(register256_4_kout5), .kin6(register256_4_kout6),
    .kin7(register256_4_kout7), .kin8(register256_4_kout8), .kin9(register256_4_kout9),
    .kin10(register256_4_kout10), .kin11(register256_4_kout11), .kin12(register256_4_kout12),
    .kin13(register256_4_kout13), .kin14(register256_4_kout14), .kin15(register256_4_kout15),
    .turn_number(4'b0100), .out0(one_turn_4_out0), .out1(one_turn_4_out1), .out2(one_turn_4_out2),
    .out3(one_turn_4_out3), .out4(one_turn_4_out4), .out5(one_turn_4_out5), .out6(one_turn_4_out6),
    .out7(one_turn_4_out7), .out8(one_turn_4_out8), .out9(one_turn_4_out9), .out10(one_turn_4_out10),
    .out11(one_turn_4_out11), .out12(one_turn_4_out12), .out13(one_turn_4_out13), .out14(one_turn_4_out14),
    .out15(one_turn_4_out15), .kout0(one_turn_4_kout0), .kout1(one_turn_4_kout1), .kout2(one_turn_4_kout2),
    .kout3(one_turn_4_kout3), .kout4(one_turn_4_kout4), .kout4_2(one_turn_4_kout4_2),
    .kout6(one_turn_4_kout6), .kout7(one_turn_4_kout7), .kout8(one_turn_4_kout8), .kout9(one_turn_4_kout9),
    .kout10(one_turn_4_kout10), .kout11(one_turn_4_kout11), .kout12(one_turn_4_kout12),
    .kout13(one_turn_4_kout13), .kout14(one_turn_4_kout14), .kout15(one_turn_4_kout15));
  one_turn one_turn_5 (
    .in0(register256_5_out0), .in1(register256_5_out1), .in2(register256_5_out2), .in3(register256_5_out3),
    .in4(register256_5_out4), .in5(register256_5_out5), .in6(register256_5_out6), .in7(register256_5_out7),
    .in8(register256_5_out8), .in9(register256_5_out9), .in10(register256_5_out10),
    .in11(register256_5_out11), .in12(register256_5_out12), .in13(register256_5_out13),
    .in14(register256_5_out14), .in15(register256_5_out15), .kin0(register256_5_kout0),
    .kin1(register256_5_kout1), .kin2(register256_5_kout2), .kin3(register256_5_kout3),
    .kin4(register256_5_kout4), .kin4_2(register256_5_kout5), .kin6(register256_5_kout6),
    .kin7(register256_5_kout7), .kin8(register256_5_kout8), .kin9(register256_5_kout9),
    .kin10(register256_5_kout10), .kin11(register256_5_kout11), .kin12(register256_5_kout12),
    .kin13(register256_5_kout13), .kin14(register256_5_kout14), .kin15(register256_5_kout15),
    .turn_number(4'b0101), .out0(one_turn_5_out0), .out1(one_turn_5_out1), .out2(one_turn_5_out2),
    .out3(one_turn_5_out3), .out4(one_turn_5_out4), .out5(one_turn_5_out5), .out6(one_turn_5_out6),
    .out7(one_turn_5_out7), .out8(one_turn_5_out8), .out9(one_turn_5_out9), .out10(one_turn_5_out10),
    .out11(one_turn_5_out11), .out12(one_turn_5_out12), .out13(one_turn_5_out13), .out14(one_turn_5_out14),
    .out15(one_turn_5_out15), .kout0(one_turn_5_kout0), .kout1(one_turn_5_kout1), .kout2(one_turn_5_kout2),
    .kout3(one_turn_5_kout3), .kout4(one_turn_5_kout4), .kout4_2(one_turn_5_kout4_2),
    .kout6(one_turn_5_kout6), .kout7(one_turn_5_kout7), .kout8(one_turn_5_kout8), .kout9(one_turn_5_kout9),
    .kout10(one_turn_5_kout10), .kout11(one_turn_5_kout11), .kout12(one_turn_5_kout12),
    .kout13(one_turn_5_kout13), .kout14(one_turn_5_kout14), .kout15(one_turn_5_kout15));
  register256 register256_6 (
    .in0(one_turn_5_out0), .in8(one_turn_5_out8), .in1(one_turn_5_out1), .in9(one_turn_5_out9),
    .in2(one_turn_5_out2), .in10(one_turn_5_out10), .in3(one_turn_5_out3), .in11(one_turn_5_out11),
    .in4(one_turn_5_out4), .in12(one_turn_5_out12), .in5(one_turn_5_out5), .in13(one_turn_5_out13),
    .in6(one_turn_5_out6), .in14(one_turn_5_out14), .in7(one_turn_5_out7), .in15(one_turn_5_out15),
    .kin0(one_turn_5_kout0), .kin8(one_turn_5_kout8), .kin1(one_turn_5_kout1), .kin9(one_turn_5_kout9),
    .kin2(one_turn_5_kout2), .kin10(one_turn_5_kout10), .kin3(one_turn_5_kout3), .kin11(one_turn_5_kout11),
    .kin4(one_turn_5_kout4), .kin12(one_turn_5_kout12), .kin5(one_turn_5_kout4_2), .kin13(one_turn_5_kout13),
    .kin6(one_turn_5_kout6), .kin14(one_turn_5_kout14), .kin7(one_turn_5_kout7), .kin15(one_turn_5_kout15),
    .clk(clk), .out0(register256_6_out0), .out8(register256_6_out8), .out1(register256_6_out1),
    .out9(register256_6_out9), .out2(register256_6_out2), .out10(register256_6_out10),
    .out3(register256_6_out3), .out11(register256_6_out11), .out4(register256_6_out4),
    .out12(register256_6_out12), .out5(register256_6_out5), .out13(register256_6_out13),
    .out6(register256_6_out6), .out14(register256_6_out14), .out7(register256_6_out7),
    .out15(register256_6_out15), .kout0(register256_6_kout0), .kout8(register256_6_kout8),
    .kout1(register256_6_kout1), .kout9(register256_6_kout9), .kout2(register256_6_kout2),
    .kout10(register256_6_kout10), .kout3(register256_6_kout3), .kout11(register256_6_kout11),
    .kout4(register256_6_kout4), .kout12(register256_6_kout12), .kout5(register256_6_kout5),
    .kout13(register256_6_kout13), .kout6(register256_6_kout6), .kout14(register256_6_kout14),
    .kout7(register256_6_kout7), .kout15(register256_6_kout15));
  one_turn one_turn_6 (
    .in0(register256_6_out0), .in1(register256_6_out1), .in2(register256_6_out2), .in3(register256_6_out3),
    .in4(register256_6_out4), .in5(register256_6_out5), .in6(register256_6_out6), .in7(register256_6_out7),
    .in8(register256_6_out8), .in9(register256_6_out9), .in10(register256_6_out10),
    .in11(register256_6_out11), .in12(register256_6_out12), .in13(register256_6_out13),
    .in14(register256_6_out14), .in15(register256_6_out15), .kin0(register256_6_kout0),
    .kin1(register256_6_kout1), .kin2(register256_6_kout2), .kin3(register256_6_kout3),
    .kin4(register256_6_kout4), .kin4_2(register256_6_kout5), .kin6(register256_6_kout6),
    .kin7(register256_6_kout7), .kin8(register256_6_kout8), .kin9(register256_6_kout9),
    .kin10(register256_6_kout10), .kin11(register256_6_kout11), .kin12(register256_6_kout12),
    .kin13(register256_6_kout13), .kin14(register256_6_kout14), .kin15(register256_6_kout15),
    .turn_number(4'b0110), .out0(one_turn_6_out0), .out1(one_turn_6_out1), .out2(one_turn_6_out2),
    .out3(one_turn_6_out3), .out4(one_turn_6_out4), .out5(one_turn_6_out5), .out6(one_turn_6_out6),
    .out7(one_turn_6_out7), .out8(one_turn_6_out8), .out9(one_turn_6_out9), .out10(one_turn_6_out10),
    .out11(one_turn_6_out11), .out12(one_turn_6_out12), .out13(one_turn_6_out13), .out14(one_turn_6_out14),
    .out15(one_turn_6_out15), .kout0(one_turn_6_kout0), .kout1(one_turn_6_kout1), .kout2(one_turn_6_kout2),
    .kout3(one_turn_6_kout3), .kout4(one_turn_6_kout4), .kout4_2(one_turn_6_kout4_2),
    .kout6(one_turn_6_kout6), .kout7(one_turn_6_kout7), .kout8(one_turn_6_kout8), .kout9(one_turn_6_kout9),
    .kout10(one_turn_6_kout10), .kout11(one_turn_6_kout11), .kout12(one_turn_6_kout12),
    .kout13(one_turn_6_kout13), .kout14(one_turn_6_kout14), .kout15(one_turn_6_kout15));
  register256 register256_7 (
    .in0(one_turn_6_out0), .in8(one_turn_6_out8), .in1(one_turn_6_out1), .in9(one_turn_6_out9),
    .in2(one_turn_6_out2), .in10(one_turn_6_out10), .in3(one_turn_6_out3), .in11(one_turn_6_out11),
    .in4(one_turn_6_out4), .in12(one_turn_6_out12), .in5(one_turn_6_out5), .in13(one_turn_6_out13),
    .in6(one_turn_6_out6), .in14(one_turn_6_out14), .in7(one_turn_6_out7), .in15(one_turn_6_out15),
    .kin0(one_turn_6_kout0), .kin8(one_turn_6_kout8), .kin1(one_turn_6_kout1), .kin9(one_turn_6_kout9),
    .kin2(one_turn_6_kout2), .kin10(one_turn_6_kout10), .kin3(one_turn_6_kout3), .kin11(one_turn_6_kout11),
    .kin4(one_turn_6_kout4), .kin12(one_turn_6_kout12), .kin5(one_turn_6_kout4_2), .kin13(one_turn_6_kout13),
    .kin6(one_turn_6_kout6), .kin14(one_turn_6_kout14), .kin7(one_turn_6_kout7), .kin15(one_turn_6_kout15),
    .clk(clk), .out0(register256_7_out0), .out8(register256_7_out8), .out1(register256_7_out1),
    .out9(register256_7_out9), .out2(register256_7_out2), .out10(register256_7_out10),
    .out3(register256_7_out3), .out11(register256_7_out11), .out4(register256_7_out4),
    .out12(register256_7_out12), .out5(register256_7_out5), .out13(register256_7_out13),
    .out6(register256_7_out6), .out14(register256_7_out14), .out7(register256_7_out7),
    .out15(register256_7_out15), .kout0(register256_7_kout0), .kout8(register256_7_kout8),
    .kout1(register256_7_kout1), .kout9(register256_7_kout9), .kout2(register256_7_kout2),
    .kout10(register256_7_kout10), .kout3(register256_7_kout3), .kout11(register256_7_kout11),
    .kout4(register256_7_kout4), .kout12(register256_7_kout12), .kout5(register256_7_kout5),
    .kout13(register256_7_kout13), .kout6(register256_7_kout6), .kout14(register256_7_kout14),
    .kout7(register256_7_kout7), .kout15(register256_7_kout15));
  one_turn one_turn_7 (
    .in0(register256_7_out0), .in1(register256_7_out1), .in2(register256_7_out2), .in3(register256_7_out3),
    .in4(register256_7_out4), .in5(register256_7_out5), .in6(register256_7_out6), .in7(register256_7_out7),
    .in8(register256_7_out8), .in9(register256_7_out9), .in10(register256_7_out10),
    .in11(register256_7_out11), .in12(register256_7_out12), .in13(register256_7_out13),
    .in14(register256_7_out14), .in15(register256_7_out15), .kin0(register256_7_kout0),
    .kin1(register256_7_kout1), .kin2(register256_7_kout2), .kin3(register256_7_kout3),
    .kin4(register256_7_kout4), .kin4_2(register256_7_kout5), .kin6(register256_7_kout6),
    .kin7(register256_7_kout7), .kin8(register256_7_kout8), .kin9(register256_7_kout9),
    .kin10(register256_7_kout10), .kin11(register256_7_kout11), .kin12(register256_7_kout12),
    .kin13(register256_7_kout13), .kin14(register256_7_kout14), .kin15(register256_7_kout15),
    .turn_number(4'b0111), .out0(one_turn_7_out0), .out1(one_turn_7_out1), .out2(one_turn_7_out2),
    .out3(one_turn_7_out3), .out4(one_turn_7_out4), .out5(one_turn_7_out5), .out6(one_turn_7_out6),
    .out7(one_turn_7_out7), .out8(one_turn_7_out8), .out9(one_turn_7_out9), .out10(one_turn_7_out10),
    .out11(one_turn_7_out11), .out12(one_turn_7_out12), .out13(one_turn_7_out13), .out14(one_turn_7_out14),
    .out15(one_turn_7_out15), .kout0(one_turn_7_kout0), .kout1(one_turn_7_kout1), .kout2(one_turn_7_kout2),
    .kout3(one_turn_7_kout3), .kout4(one_turn_7_kout4), .kout4_2(one_turn_7_kout4_2),
    .kout6(one_turn_7_kout6), .kout7(one_turn_7_kout7), .kout8(one_turn_7_kout8), .kout9(one_turn_7_kout9),
    .kout10(one_turn_7_kout10), .kout11(one_turn_7_kout11), .kout12(one_turn_7_kout12),
    .kout13(one_turn_7_kout13), .kout14(one_turn_7_kout14), .kout15(one_turn_7_kout15));
  register256 register256_8 (
    .in0(one_turn_7_out0), .in8(one_turn_7_out8), .in1(one_turn_7_out1), .in9(one_turn_7_out9),
    .in2(one_turn_7_out2), .in10(one_turn_7_out10), .in3(one_turn_7_out3), .in11(one_turn_7_out11),
    .in4(one_turn_7_out4), .in12(one_turn_7_out12), .in5(one_turn_7_out5), .in13(one_turn_7_out13),
    .in6(one_turn_7_out6), .in14(one_turn_7_out14), .in7(one_turn_7_out7), .in15(one_turn_7_out15),
    .kin0(one_turn_7_kout0), .kin8(one_turn_7_kout8), .kin1(one_turn_7_kout1), .kin9(one_turn_7_kout9),
    .kin2(one_turn_7_kout2), .kin10(one_turn_7_kout10), .kin3(one_turn_7_kout3), .kin11(one_turn_7_kout11),
    .kin4(one_turn_7_kout4), .kin12(one_turn_7_kout12), .kin5(one_turn_7_kout4_2), .kin13(one_turn_7_kout13),
    .kin6(one_turn_7_kout6), .kin14(one_turn_7_kout14), .kin7(one_turn_7_kout7), .kin15(one_turn_7_kout15),
    .clk(clk), .out0(register256_8_out0), .out8(register256_8_out8), .out1(register256_8_out1),
    .out9(register256_8_out9), .out2(register256_8_out2), .out10(register256_8_out10),
    .out3(register256_8_out3), .out11(register256_8_out11), .out4(register256_8_out4),
    .out12(register256_8_out12), .out5(register256_8_out5), .out13(register256_8_out13),
    .out6(register256_8_out6), .out14(register256_8_out14), .out7(register256_8_out7),
    .out15(register256_8_out15), .kout0(register256_8_kout0), .kout8(register256_8_kout8),
    .kout1(register256_8_kout1), .kout9(register256_8_kout9), .kout2(register256_8_kout2),
    .kout10(register256_8_kout10), .kout3(register256_8_kout3), .kout11(register256_8_kout11),
    .kout4(register256_8_kout4), .kout12(register256_8_kout12), .kout5(register256_8_kout5),
    .kout13(register256_8_kout13), .kout6(register256_8_kout6), .kout14(register256_8_kout14),
    .kout7(register256_8_kout7), .kout15(register256_8_kout15));
  register256 register256_9 (
    .in0(one_turn_8_out0), .in8(one_turn_8_out8), .in1(one_turn_8_out1), .in9(one_turn_8_out9),
    .in2(one_turn_8_out2), .in10(one_turn_8_out10), .in3(one_turn_8_out3), .in11(one_turn_8_out11),
    .in4(one_turn_8_out4), .in12(one_turn_8_out12), .in5(one_turn_8_out5), .in13(one_turn_8_out13),
    .in6(one_turn_8_out6), .in14(one_turn_8_out14), .in7(one_turn_8_out7), .in15(one_turn_8_out15),
    .kin0(one_turn_8_kout0), .kin8(one_turn_8_kout8), .kin1(one_turn_8_kout1), .kin9(one_turn_8_kout9),
    .kin2(one_turn_8_kout2), .kin10(one_turn_8_kout10), .kin3(one_turn_8_kout3), .kin11(one_turn_8_kout11),
    .kin4(one_turn_8_kout4), .kin12(one_turn_8_kout12), .kin5(one_turn_8_kout4_2), .kin13(one_turn_8_kout13),
    .kin6(one_turn_8_kout6), .kin14(one_turn_8_kout14), .kin7(one_turn_8_kout7), .kin15(one_turn_8_kout15),
    .clk(clk), .out0(register256_9_out0), .out8(register256_9_out8), .out1(register256_9_out1),
    .out9(register256_9_out9), .out2(register256_9_out2), .out10(register256_9_out10),
    .out3(register256_9_out3), .out11(register256_9_out11), .out4(register256_9_out4),
    .out12(register256_9_out12), .out5(register256_9_out5), .out13(register256_9_out13),
    .out6(register256_9_out6), .out14(register256_9_out14), .out7(register256_9_out7),
    .out15(register256_9_out15), .kout0(register256_9_kout0), .kout8(register256_9_kout8),
    .kout1(register256_9_kout1), .kout9(register256_9_kout9), .kout2(register256_9_kout2),
    .kout10(register256_9_kout10), .kout3(register256_9_kout3), .kout11(register256_9_kout11),
    .kout4(register256_9_kout4), .kout12(register256_9_kout12), .kout5(register256_9_kout5),
    .kout13(register256_9_kout13), .kout6(register256_9_kout6), .kout14(register256_9_kout14),
    .kout7(register256_9_kout7), .kout15(register256_9_kout15));
  one_turn one_turn_8 (
    .in0(register256_8_out0), .in1(register256_8_out1), .in2(register256_8_out2), .in3(register256_8_out3),
    .in4(register256_8_out4), .in5(register256_8_out5), .in6(register256_8_out6), .in7(register256_8_out7),
    .in8(register256_8_out8), .in9(register256_8_out9), .in10(register256_8_out10),
    .in11(register256_8_out11), .in12(register256_8_out12), .in13(register256_8_out13),
    .in14(register256_8_out14), .in15(register256_8_out15), .kin0(register256_8_kout0),
    .kin1(register256_8_kout1), .kin2(register256_8_kout2), .kin3(register256_8_kout3),
    .kin4(register256_8_kout4), .kin4_2(register256_8_kout5), .kin6(register256_8_kout6),
    .kin7(register256_8_kout7), .kin8(register256_8_kout8), .kin9(register256_8_kout9),
    .kin10(register256_8_kout10), .kin11(register256_8_kout11), .kin12(register256_8_kout12),
    .kin13(register256_8_kout13), .kin14(register256_8_kout14), .kin15(register256_8_kout15),
    .turn_number(4'b1000), .out0(one_turn_8_out0), .out1(one_turn_8_out1), .out2(one_turn_8_out2),
    .out3(one_turn_8_out3), .out4(one_turn_8_out4), .out5(one_turn_8_out5), .out6(one_turn_8_out6),
    .out7(one_turn_8_out7), .out8(one_turn_8_out8), .out9(one_turn_8_out9), .out10(one_turn_8_out10),
    .out11(one_turn_8_out11), .out12(one_turn_8_out12), .out13(one_turn_8_out13), .out14(one_turn_8_out14),
    .out15(one_turn_8_out15), .kout0(one_turn_8_kout0), .kout1(one_turn_8_kout1), .kout2(one_turn_8_kout2),
    .kout3(one_turn_8_kout3), .kout4(one_turn_8_kout4), .kout4_2(one_turn_8_kout4_2),
    .kout6(one_turn_8_kout6), .kout7(one_turn_8_kout7), .kout8(one_turn_8_kout8), .kout9(one_turn_8_kout9),
    .kout10(one_turn_8_kout10), .kout11(one_turn_8_kout11), .kout12(one_turn_8_kout12),
    .kout13(one_turn_8_kout13), .kout14(one_turn_8_kout14), .kout15(one_turn_8_kout15));
  one_turn one_turn_9 (
    .in0(register256_9_out0), .in1(register256_9_out1), .in2(register256_9_out2), .in3(register256_9_out3),
    .in4(register256_9_out4), .in5(register256_9_out5), .in6(register256_9_out6), .in7(register256_9_out7),
    .in8(register256_9_out8), .in9(register256_9_out9), .in10(register256_9_out10),
    .in11(register256_9_out11), .in12(register256_9_out12), .in13(register256_9_out13),
    .in14(register256_9_out14), .in15(register256_9_out15), .kin0(register256_9_kout0),
    .kin1(register256_9_kout1), .kin2(register256_9_kout2), .kin3(register256_9_kout3),
    .kin4(register256_9_kout4), .kin4_2(register256_9_kout5), .kin6(register256_9_kout6),
    .kin7(register256_9_kout7), .kin8(register256_9_kout8), .kin9(register256_9_kout9),
    .kin10(register256_9_kout10), .kin11(register256_9_kout11), .kin12(register256_9_kout12),
    .kin13(register256_9_kout13), .kin14(register256_9_kout14), .kin15(register256_9_kout15),
    .turn_number(4'b1001), .out0(one_turn_9_out0), .out1(one_turn_9_out1), .out2(one_turn_9_out2),
    .out3(one_turn_9_out3), .out4(one_turn_9_out4), .out5(one_turn_9_out5), .out6(one_turn_9_out6),
    .out7(one_turn_9_out7), .out8(one_turn_9_out8), .out9(one_turn_9_out9), .out10(one_turn_9_out10),
    .out11(one_turn_9_out11), .out12(one_turn_9_out12), .out13(one_turn_9_out13), .out14(one_turn_9_out14),
    .out15(one_turn_9_out15), .kout0(one_turn_9_kout0), .kout1(one_turn_9_kout1), .kout2(one_turn_9_kout2),
    .kout3(one_turn_9_kout3), .kout4(one_turn_9_kout4), .kout4_2(one_turn_9_kout4_2),
    .kout6(one_turn_9_kout6), .kout7(one_turn_9_kout7), .kout8(one_turn_9_kout8), .kout9(one_turn_9_kout9),
    .kout10(one_turn_9_kout10), .kout11(one_turn_9_kout11), .kout12(one_turn_9_kout12),
    .kout13(one_turn_9_kout13), .kout14(one_turn_9_kout14), .kout15(one_turn_9_kout15));
  register256 register256_10 (
    .in0(one_turn_9_out0), .in8(one_turn_9_out8), .in1(one_turn_9_out1), .in9(one_turn_9_out9),
    .in2(one_turn_9_out2), .in10(one_turn_9_out10), .in3(one_turn_9_out3), .in11(one_turn_9_out11),
    .in4(one_turn_9_out4), .in12(one_turn_9_out12), .in5(one_turn_9_out5), .in13(one_turn_9_out13),
    .in6(one_turn_9_out6), .in14(one_turn_9_out14), .in7(one_turn_9_out7), .in15(one_turn_9_out15),
    .kin0(one_turn_9_kout0), .kin8(one_turn_9_kout8), .kin1(one_turn_9_kout1), .kin9(one_turn_9_kout9),
    .kin2(one_turn_9_kout2), .kin10(one_turn_9_kout10), .kin3(one_turn_9_kout3), .kin11(one_turn_9_kout11),
    .kin4(one_turn_9_kout4), .kin12(one_turn_9_kout12), .kin5(one_turn_9_kout4_2), .kin13(one_turn_9_kout13),
    .kin6(one_turn_9_kout6), .kin14(one_turn_9_kout14), .kin7(one_turn_9_kout7), .kin15(one_turn_9_kout15),
    .clk(clk), .out0(register256_10_out0), .out8(register256_10_out8), .out1(register256_10_out1),
    .out9(register256_10_out9), .out2(register256_10_out2), .out10(register256_10_out10),
    .out3(register256_10_out3), .out11(register256_10_out11), .out4(register256_10_out4),
    .out12(register256_10_out12), .out5(register256_10_out5), .out13(register256_10_out13),
    .out6(register256_10_out6), .out14(register256_10_out14), .out7(register256_10_out7),
    .out15(register256_10_out15), .kout0(register256_10_kout0), .kout8(register256_10_kout8),
    .kout1(register256_10_kout1), .kout9(register256_10_kout9), .kout2(register256_10_kout2),
    .kout10(register256_10_kout10), .kout3(register256_10_kout3), .kout11(register256_10_kout11),
    .kout4(register256_10_kout4), .kout12(register256_10_kout12), .kout5(register256_10_kout5),
    .kout13(register256_10_kout13), .kout6(register256_10_kout6), .kout14(register256_10_kout14),
    .kout7(register256_10_kout7), .kout15(register256_10_kout15));
  last_turn last_turn_1 (
    .in0(register256_10_out0), .in1(register256_10_out1), .in2(register256_10_out2),
    .in3(register256_10_out3), .in4(register256_10_out4), .in5(register256_10_out5),
    .in6(register256_10_out6), .in7(register256_10_out7), .in8(register256_10_out8),
    .in9(register256_10_out9), .in10(register256_10_out10), .in11(register256_10_out11),
    .in12(register256_10_out12), .in13(register256_10_out13), .in14(register256_10_out14),
    .in15(register256_10_out15), .kin0(register256_10_kout0), .kin1(register256_10_kout1),
    .kin2(register256_10_kout2), .kin3(register256_10_kout3), .kin4(register256_10_kout4),
    .kin4_2(register256_10_kout5), .kin6(register256_10_kout6), .kin7(register256_10_kout7),
    .kin8(register256_10_kout8), .kin9(register256_10_kout9), .kin10(register256_10_kout10),
    .kin11(register256_10_kout11), .kin12(register256_10_kout12), .kin13(register256_10_kout13),
    .kin14(register256_10_kout14), .kin15(register256_10_kout15), .out0(c0[31:24]), .out1(c0[23:16]),
    .out2(c0[15:8]), .out3(c0[7:0]), .out4(c1[31:24]), .out5(c1[23:16]), .out6(c1[15:8]), .out7(c1[7:0]),
    .out8(c2[31:24]), .out9(c2[23:16]), .out10(c2[15:8]), .out11(c2[7:0]), .out12(c3[31:24]),
    .out13(c3[23:16]), .out14(c3[15:8]), .out15(c3[7:0]));
endmodule

module first_turn (
  input  [7:0] in0,
  input  [7:0] in1,
  input  [7:0] in2,
  input  [7:0] in3,
  input  [7:0] in4,
  input  [7:0] in5,
  input  [7:0] in6,
  input  [7:0] in7,
  input  [7:0] in8,
  input  [7:0] in9,
  input  [7:0] in10,
  input  [7:0] in11,
  input  [7:0] in12,
  input  [7:0] in13,
  input  [7:0] in14,
  input  [7:0] in15,
  input  [7:0] kin0,
  input  [7:0] kin1,
  input  [7:0] kin2,
  input  [7:0] kin3,
  input  [7:0] kin4,
  input  [7:0] kin4_2,
  input  [7:0] kin6,
  input  [7:0] kin7,
  input  [7:0] kin8,
  input  [7:0] kin9,
  input  [7:0] kin10,
  input  [7:0] kin11,
  input  [7:0] kin12,
  input  [7:0] kin13,
  input  [7:0] kin14,
  input  [7:0] kin15,
  output [7:0] out0,
  output [7:0] out1,
  output [7:0] out2,
  output [7:0] out3,
  output [7:0] out4,
  output [7:0] out5,
  output [7:0] out6,
  output [7:0] out7,
  output [7:0] out8,
  output [7:0] out9,
  output [7:0] out10,
  output [7:0] out11,
  output [7:0] out12,
  output [7:0] out13,
  output [7:0] out14,
  output [7:0] out15,
  output [7:0] kout0,
  output [7:0] kout1,
  output [7:0] kout2,
  output [7:0] kout3,
  output [7:0] kout4,
  output [7:0] kout4_2,
  output [7:0] kout6,
  output [7:0] kout7,
  output [7:0] kout8,
  output [7:0] kout9,
  output [7:0] kout10,
  output [7:0] kout11,
  output [7:0] kout12,
  output [7:0] kout13,
  output [7:0] kout14,
  output [7:0] kout15
);

  subkey_add_gen subkey_add_gen_1 (
    .in0(in0), .in1(in1), .in2(in2), .in3(in3), .in4(in4), .in5(in5), .in6(in6), .in7(in7), .in8(in8),
    .in9(in9), .in10(in10), .in11(in11), .in12(in12), .in13(in13), .in14(in14), .in15(in15), .kin0(kin0),
    .kin1(kin1), .kin2(kin2), .kin3(kin3), .kin4(kin4), .kin4_2(kin4_2), .kin6(kin6), .kin7(kin7),
    .kin8(kin8), .kin9(kin9), .kin10(kin10), .kin11(kin11), .kin12(kin12), .kin13(kin13), .kin14(kin14),
    .kin15(kin15), .turn_number(4'b0000), .out0(out0), .out1(out1), .out2(out2), .out3(out3), .out4(out4),
    .out5(out5), .out6(out6), .out7(out7), .out8(out8), .out9(out9), .out10(out10), .out11(out11),
    .out12(out12), .out13(out13), .out14(out14), .out15(out15), .kout0(kout0), .kout1(kout1), .kout2(kout2),
    .kout3(kout3), .kout4(kout4), .kout4_2(kout4_2), .kout6(kout6), .kout7(kout7), .kout8(kout8),
    .kout9(kout9), .kout10(kout10), .kout11(kout11), .kout12(kout12), .kout13(kout13), .kout14(kout14),
    .kout15(kout15));
endmodule

module one_turn (
  input  [7:0] in0,
  input  [7:0] in1,
  input  [7:0] in2,
  input  [7:0] in3,
  input  [7:0] in4,
  input  [7:0] in5,
  input  [7:0] in6,
  input  [7:0] in7,
  input  [7:0] in8,
  input  [7:0] in9,
  input  [7:0] in10,
  input  [7:0] in11,
  input  [7:0] in12,
  input  [7:0] in13,
  input  [7:0] in14,
  input  [7:0] in15,
  input  [7:0] kin0,
  input  [7:0] kin1,
  input  [7:0] kin2,
  input  [7:0] kin3,
  input  [7:0] kin4,
  input  [7:0] kin4_2,
  input  [7:0] kin6,
  input  [7:0] kin7,
  input  [7:0] kin8,
  input  [7:0] kin9,
  input  [7:0] kin10,
  input  [7:0] kin11,
  input  [7:0] kin12,
  input  [7:0] kin13,
  input  [7:0] kin14,
  input  [7:0] kin15,
  input  [3:0] turn_number,
  output [7:0] out0,
  output [7:0] out1,
  output [7:0] out2,
  output [7:0] out3,
  output [7:0] out4,
  output [7:0] out5,
  output [7:0] out6,
  output [7:0] out7,
  output [7:0] out8,
  output [7:0] out9,
  output [7:0] out10,
  output [7:0] out11,
  output [7:0] out12,
  output [7:0] out13,
  output [7:0] out14,
  output [7:0] out15,
  output [7:0] kout0,
  output [7:0] kout1,
  output [7:0] kout2,
  output [7:0] kout3,
  output [7:0] kout4,
  output [7:0] kout4_2,
  output [7:0] kout6,
  output [7:0] kout7,
  output [7:0] kout8,
  output [7:0] kout9,
  output [7:0] kout10,
  output [7:0] kout11,
  output [7:0] kout12,
  output [7:0] kout13,
  output [7:0] kout14,
  output [7:0] kout15
);

  wire [7:0] byte_substitute_1_out0, byte_substitute_1_out1, byte_substitute_1_out2, byte_substitute_1_out3,
       byte_substitute_1_out4, byte_substitute_1_out5, byte_substitute_1_out6, byte_substitute_1_out7,
       byte_substitute_1_out8, byte_substitute_1_out9, byte_substitute_1_out10, byte_substitute_1_out11,
       byte_substitute_1_out12, byte_substitute_1_out13, byte_substitute_1_out14, byte_substitute_1_out15,
       column_mix_1_out0, column_mix_1_out1, column_mix_1_out2, column_mix_1_out3, column_mix_1_out4,
       column_mix_1_out5, column_mix_1_out6, column_mix_1_out7, column_mix_1_out8, column_mix_1_out9,
       column_mix_1_out10, column_mix_1_out11, column_mix_1_out12, column_mix_1_out13, column_mix_1_out14,
       column_mix_1_out15, raw_shift_1_out0, raw_shift_1_out1, raw_shift_1_out2, raw_shift_1_out3,
       raw_shift_1_out4, raw_shift_1_out5, raw_shift_1_out6, raw_shift_1_out7, raw_shift_1_out8,
       raw_shift_1_out9, raw_shift_1_out10, raw_shift_1_out11, raw_shift_1_out12, raw_shift_1_out13,
       raw_shift_1_out14, raw_shift_1_out15;

  byte_substitute byte_substitute_1 (
    .in0(in0), .in1(in1), .in2(in2), .in3(in3), .in4(in4), .in5(in5), .in6(in6), .in7(in7), .in8(in8),
    .in9(in9), .in10(in10), .in11(in11), .in12(in12), .in13(in13), .in14(in14), .in15(in15),
    .out0(byte_substitute_1_out0), .out1(byte_substitute_1_out1), .out2(byte_substitute_1_out2),
    .out3(byte_substitute_1_out3), .out4(byte_substitute_1_out4), .out5(byte_substitute_1_out5),
    .out6(byte_substitute_1_out6), .out7(byte_substitute_1_out7), .out8(byte_substitute_1_out8),
    .out9(byte_substitute_1_out9), .out10(byte_substitute_1_out10), .out11(byte_substitute_1_out11),
    .out12(byte_substitute_1_out12), .out13(byte_substitute_1_out13), .out14(byte_substitute_1_out14),
    .out15(byte_substitute_1_out15));
  raw_shift raw_shift_1 (
    .in0(byte_substitute_1_out0), .in4(byte_substitute_1_out4), .in8(byte_substitute_1_out8),
    .in12(byte_substitute_1_out12), .in1(byte_substitute_1_out1), .in5(byte_substitute_1_out5),
    .in9(byte_substitute_1_out9), .in13(byte_substitute_1_out13), .in2(byte_substitute_1_out2),
    .in6(byte_substitute_1_out6), .in10(byte_substitute_1_out10), .in14(byte_substitute_1_out14),
    .in3(byte_substitute_1_out3), .in7(byte_substitute_1_out7), .in11(byte_substitute_1_out11),
    .in15(byte_substitute_1_out15), .out0(raw_shift_1_out0), .out4(raw_shift_1_out4),
    .out8(raw_shift_1_out8), .out12(raw_shift_1_out12), .out1(raw_shift_1_out1), .out5(raw_shift_1_out5),
    .out9(raw_shift_1_out9), .out13(raw_shift_1_out13), .out2(raw_shift_1_out2), .out6(raw_shift_1_out6),
    .out10(raw_shift_1_out10), .out14(raw_shift_1_out14), .out3(raw_shift_1_out3), .out7(raw_shift_1_out7),
    .out11(raw_shift_1_out11), .out15(raw_shift_1_out15));
  column_mix column_mix_1 (
    .in0(raw_shift_1_out0), .in1(raw_shift_1_out1), .in2(raw_shift_1_out2), .in3(raw_shift_1_out3),
    .in4(raw_shift_1_out4), .in5(raw_shift_1_out5), .in6(raw_shift_1_out6), .in7(raw_shift_1_out7),
    .in8(raw_shift_1_out8), .in9(raw_shift_1_out9), .in10(raw_shift_1_out10), .in11(raw_shift_1_out11),
    .in12(raw_shift_1_out12), .in13(raw_shift_1_out13), .in14(raw_shift_1_out14), .in15(raw_shift_1_out15),
    .out0(column_mix_1_out0), .out1(column_mix_1_out1), .out2(column_mix_1_out2), .out3(column_mix_1_out3),
    .out4(column_mix_1_out4), .out5(column_mix_1_out5), .out6(column_mix_1_out6), .out7(column_mix_1_out7),
    .out8(column_mix_1_out8), .out9(column_mix_1_out9), .out10(column_mix_1_out10),
    .out11(column_mix_1_out11), .out12(column_mix_1_out12), .out13(column_mix_1_out13),
    .out14(column_mix_1_out14), .out15(column_mix_1_out15));
  subkey_add_gen subkey_add_gen_1 (
    .in0(column_mix_1_out0), .in1(column_mix_1_out1), .in2(column_mix_1_out2), .in3(column_mix_1_out3),
    .in4(column_mix_1_out4), .in5(column_mix_1_out5), .in6(column_mix_1_out6), .in7(column_mix_1_out7),
    .in8(column_mix_1_out8), .in9(column_mix_1_out9), .in10(column_mix_1_out10), .in11(column_mix_1_out11),
    .in12(column_mix_1_out12), .in13(column_mix_1_out13), .in14(column_mix_1_out14),
    .in15(column_mix_1_out15), .kin0(kin0), .kin1(kin1), .kin2(kin2), .kin3(kin3), .kin4(kin4),
    .kin4_2(kin4_2), .kin6(kin6), .kin7(kin7), .kin8(kin8), .kin9(kin9), .kin10(kin10), .kin11(kin11),
    .kin12(kin12), .kin13(kin13), .kin14(kin14), .kin15(kin15), .turn_number(turn_number), .out0(out0),
    .out1(out1), .out2(out2), .out3(out3), .out4(out4), .out5(out5), .out6(out6), .out7(out7), .out8(out8),
    .out9(out9), .out10(out10), .out11(out11), .out12(out12), .out13(out13), .out14(out14), .out15(out15),
    .kout0(kout0), .kout1(kout1), .kout2(kout2), .kout3(kout3), .kout4(kout4), .kout4_2(kout4_2),
    .kout6(kout6), .kout7(kout7), .kout8(kout8), .kout9(kout9), .kout10(kout10), .kout11(kout11),
    .kout12(kout12), .kout13(kout13), .kout14(kout14), .kout15(kout15));
endmodule

module last_turn (
  input  [7:0] in0,
  input  [7:0] in1,
  input  [7:0] in2,
  input  [7:0] in3,
  input  [7:0] in4,
  input  [7:0] in5,
  input  [7:0] in6,
  input  [7:0] in7,
  input  [7:0] in8,
  input  [7:0] in9,
  input  [7:0] in10,
  input  [7:0] in11,
  input  [7:0] in12,
  input  [7:0] in13,
  input  [7:0] in14,
  input  [7:0] in15,
  input  [7:0] kin0,
  input  [7:0] kin1,
  input  [7:0] kin2,
  input  [7:0] kin3,
  input  [7:0] kin4,
  input  [7:0] kin4_2,
  input  [7:0] kin6,
  input  [7:0] kin7,
  input  [7:0] kin8,
  input  [7:0] kin9,
  input  [7:0] kin10,
  input  [7:0] kin11,
  input  [7:0] kin12,
  input  [7:0] kin13,
  input  [7:0] kin14,
  input  [7:0] kin15,
  output [7:0] out0,
  output [7:0] out1,
  output [7:0] out2,
  output [7:0] out3,
  output [7:0] out4,
  output [7:0] out5,
  output [7:0] out6,
  output [7:0] out7,
  output [7:0] out8,
  output [7:0] out9,
  output [7:0] out10,
  output [7:0] out11,
  output [7:0] out12,
  output [7:0] out13,
  output [7:0] out14,
  output [7:0] out15
);

  wire [7:0] byte_substitute_1_out0, byte_substitute_1_out1, byte_substitute_1_out2, byte_substitute_1_out3,
       byte_substitute_1_out4, byte_substitute_1_out5, byte_substitute_1_out6, byte_substitute_1_out7,
       byte_substitute_1_out8, byte_substitute_1_out9, byte_substitute_1_out10, byte_substitute_1_out11,
       byte_substitute_1_out12, byte_substitute_1_out13, byte_substitute_1_out14, byte_substitute_1_out15,
       raw_shift_1_out0, raw_shift_1_out1, raw_shift_1_out2, raw_shift_1_out3, raw_shift_1_out4,
       raw_shift_1_out5, raw_shift_1_out6, raw_shift_1_out7, raw_shift_1_out8, raw_shift_1_out9,
       raw_shift_1_out10, raw_shift_1_out11, raw_shift_1_out12, raw_shift_1_out13, raw_shift_1_out14,
       raw_shift_1_out15;

  raw_shift raw_shift_1 (
    .in0(byte_substitute_1_out0), .in4(byte_substitute_1_out4), .in8(byte_substitute_1_out8),
    .in12(byte_substitute_1_out12), .in1(byte_substitute_1_out1), .in5(byte_substitute_1_out5),
    .in9(byte_substitute_1_out9), .in13(byte_substitute_1_out13), .in2(byte_substitute_1_out2),
    .in6(byte_substitute_1_out6), .in10(byte_substitute_1_out10), .in14(byte_substitute_1_out14),
    .in3(byte_substitute_1_out3), .in7(byte_substitute_1_out7), .in11(byte_substitute_1_out11),
    .in15(byte_substitute_1_out15), .out0(raw_shift_1_out0), .out4(raw_shift_1_out4),
    .out8(raw_shift_1_out8), .out12(raw_shift_1_out12), .out1(raw_shift_1_out1), .out5(raw_shift_1_out5),
    .out9(raw_shift_1_out9), .out13(raw_shift_1_out13), .out2(raw_shift_1_out2), .out6(raw_shift_1_out6),
    .out10(raw_shift_1_out10), .out14(raw_shift_1_out14), .out3(raw_shift_1_out3), .out7(raw_shift_1_out7),
    .out11(raw_shift_1_out11), .out15(raw_shift_1_out15));
  byte_substitute byte_substitute_1 (
    .in0(in0), .in1(in1), .in2(in2), .in3(in3), .in4(in4), .in5(in5), .in6(in6), .in7(in7), .in8(in8),
    .in9(in9), .in10(in10), .in11(in11), .in12(in12), .in13(in13), .in14(in14), .in15(in15),
    .out0(byte_substitute_1_out0), .out1(byte_substitute_1_out1), .out2(byte_substitute_1_out2),
    .out3(byte_substitute_1_out3), .out4(byte_substitute_1_out4), .out5(byte_substitute_1_out5),
    .out6(byte_substitute_1_out6), .out7(byte_substitute_1_out7), .out8(byte_substitute_1_out8),
    .out9(byte_substitute_1_out9), .out10(byte_substitute_1_out10), .out11(byte_substitute_1_out11),
    .out12(byte_substitute_1_out12), .out13(byte_substitute_1_out13), .out14(byte_substitute_1_out14),
    .out15(byte_substitute_1_out15));
  subkey_add subkey_add_1 (
    .in0(raw_shift_1_out0), .in8(raw_shift_1_out8), .kin0(kin0), .kin8(kin8), .in1(raw_shift_1_out1),
    .in9(raw_shift_1_out9), .kin1(kin1), .kin9(kin9), .in2(raw_shift_1_out2), .in10(raw_shift_1_out10),
    .kin2(kin2), .kin10(kin10), .in3(raw_shift_1_out3), .in11(raw_shift_1_out11), .kin3(kin3), .kin11(kin11),
    .in4(raw_shift_1_out4), .in12(raw_shift_1_out12), .kin4(kin4), .kin12(kin12), .in5(raw_shift_1_out5),
    .in13(raw_shift_1_out13), .kin5(kin4_2), .kin13(kin13), .in6(raw_shift_1_out6), .in14(raw_shift_1_out14),
    .kin6(kin6), .kin14(kin14), .in7(raw_shift_1_out7), .in15(raw_shift_1_out15), .kin7(kin7), .kin15(kin15),
    .out0(out0), .out8(out8), .out1(out1), .out9(out9), .out2(out2), .out10(out10), .out3(out3),
    .out11(out11), .out4(out4), .out12(out12), .out5(out5), .out13(out13), .out6(out6), .out14(out14),
    .out7(out7), .out15(out15));
endmodule

module subkey_add_gen (
  input  [7:0] in0,
  input  [7:0] in1,
  input  [7:0] in2,
  input  [7:0] in3,
  input  [7:0] in4,
  input  [7:0] in5,
  input  [7:0] in6,
  input  [7:0] in7,
  input  [7:0] in8,
  input  [7:0] in9,
  input  [7:0] in10,
  input  [7:0] in11,
  input  [7:0] in12,
  input  [7:0] in13,
  input  [7:0] in14,
  input  [7:0] in15,
  input  [7:0] kin0,
  input  [7:0] kin1,
  input  [7:0] kin2,
  input  [7:0] kin3,
  input  [7:0] kin4,
  input  [7:0] kin4_2,
  input  [7:0] kin6,
  input  [7:0] kin7,
  input  [7:0] kin8,
  input  [7:0] kin9,
  input  [7:0] kin10,
  input  [7:0] kin11,
  input  [7:0] kin12,
  input  [7:0] kin13,
  input  [7:0] kin14,
  input  [7:0] kin15,
  input  [3:0] turn_number,
  output [7:0] out0,
  output [7:0] out1,
  output [7:0] out2,
  output [7:0] out3,
  output [7:0] out4,
  output [7:0] out5,
  output [7:0] out6,
  output [7:0] out7,
  output [7:0] out8,
  output [7:0] out9,
  output [7:0] out10,
  output [7:0] out11,
  output [7:0] out12,
  output [7:0] out13,
  output [7:0] out14,
  output [7:0] out15,
  output [7:0] kout0,
  output [7:0] kout1,
  output [7:0] kout2,
  output [7:0] kout3,
  output [7:0] kout4,
  output [7:0] kout4_2,
  output [7:0] kout6,
  output [7:0] kout7,
  output [7:0] kout8,
  output [7:0] kout9,
  output [7:0] kout10,
  output [7:0] kout11,
  output [7:0] kout12,
  output [7:0] kout13,
  output [7:0] kout14,
  output [7:0] kout15
);

  subkey_add subkey_add_1 (
    .in0(in0), .in8(in8), .kin0(kin0), .kin8(kin8), .in1(in1), .in9(in9), .kin1(kin1), .kin9(kin9),
    .in2(in2), .in10(in10), .kin2(kin2), .kin10(kin10), .in3(in3), .in11(in11), .kin3(kin3), .kin11(kin11),
    .in4(in4), .in12(in12), .kin4(kin4), .kin12(kin12), .in5(in5), .in13(in13), .kin5(kin4_2), .kin13(kin13),
    .in6(in6), .in14(in14), .kin6(kin6), .kin14(kin14), .in7(in7), .in15(in15), .kin7(kin7), .kin15(kin15),
    .out0(out0), .out8(out8), .out1(out1), .out9(out9), .out2(out2), .out10(out10), .out3(out3),
    .out11(out11), .out4(out4), .out12(out12), .out5(out5), .out13(out13), .out6(out6), .out14(out14),
    .out7(out7), .out15(out15));
  key_gen_oneturn key_gen_oneturn_1 (
    .kin0(kin0), .kin1(kin1), .kin2(kin2), .kin3(kin3), .kin4(kin4), .kin4_2(kin4_2), .kin6(kin6),
    .kin7(kin7), .kin8(kin8), .kin9(kin9), .kin10(kin10), .kin11(kin11), .kin12(kin12), .kin13(kin13),
    .kin14(kin14), .kin15(kin15), .turn_number(turn_number), .kout0(kout0), .kout1(kout1), .kout2(kout2),
    .kout3(kout3), .kout4(kout4), .kout4_2(kout4_2), .kout6(kout6), .kout7(kout7), .kout8(kout8),
    .kout9(kout9), .kout10(kout10), .kout11(kout11), .kout12(kout12), .kout13(kout13), .kout14(kout14),
    .kout15(kout15));
endmodule

module key_gen_oneturn (
  input  [7:0] kin0,
  input  [7:0] kin1,
  input  [7:0] kin2,
  input  [7:0] kin3,
  input  [7:0] kin4,
  input  [7:0] kin4_2,
  input  [7:0] kin6,
  input  [7:0] kin7,
  input  [7:0] kin8,
  input  [7:0] kin9,
  input  [7:0] kin10,
  input  [7:0] kin11,
  input  [7:0] kin12,
  input  [7:0] kin13,
  input  [7:0] kin14,
  input  [7:0] kin15,
  input  [3:0] turn_number,
  output [7:0] kout0,
  output [7:0] kout1,
  output [7:0] kout2,
  output [7:0] kout3,
  output [7:0] kout4,
  output [7:0] kout4_2,
  output [7:0] kout6,
  output [7:0] kout7,
  output [7:0] kout8,
  output [7:0] kout9,
  output [7:0] kout10,
  output [7:0] kout11,
  output [7:0] kout12,
  output [7:0] kout13,
  output [7:0] kout14,
  output [7:0] kout15
);

  wire [31:0] key_gen_g_1_out;

  key_gen_g key_gen_g_1 (.in({kin12, kin13, kin14, kin15}), .turn_number(turn_number), .out(key_gen_g_1_out));
  assign {kout0, kout1, kout2, kout3} = key_gen_g_1_out ^ {kin0, kin1, kin2, kin3};  // XOR_Gate xor_1, 32 bits wide
  assign {kout4, kout4_2, kout6, kout7} = {kout0, kout1, kout2, kout3} ^ {kin4, kin4_2, kin6, kin7};  // XOR_Gate xor_2, 32 bits wide
  assign {kout8, kout9, kout10, kout11} = {kout4, kout4_2, kout6, kout7} ^ {kin8, kin9, kin10, kin11};  // XOR_Gate xor_3, 32 bits wide
  assign {kout12, kout13, kout14, kout15} = {kout8, kout9, kout10, kout11} ^ {kin12, kin13, kin14, kin15};  // XOR_Gate xor_4, 32 bits wide
endmodule

module subkey_add (
  input  [7:0] in0,
  input  [7:0] in8,
  input  [7:0] kin0,
  input  [7:0] kin8,
  input  [7:0] in1,
  input  [7:0] in9,
  input  [7:0] kin1,
  input  [7:0] kin9,
  input  [7:0] in2,
  input  [7:0] in10,
  input  [7:0] kin2,
  input  [7:0] kin10,
  input  [7:0] in3,
  input  [7:0] in11,
  input  [7:0] kin3,
  input  [7:0] kin11,
  input  [7:0] in4,
  input  [7:0] in12,
  input  [7:0] kin4,
  input  [7:0] kin12,
  input  [7:0] in5,
  input  [7:0] in13,
  input  [7:0] kin5,
  input  [7:0] kin13,
  input  [7:0] in6,
  input  [7:0] in14,
  input  [7:0] kin6,
  input  [7:0] kin14,
  input  [7:0] in7,
  input  [7:0] in15,
  input  [7:0] kin7,
  input  [7:0] kin15,
  output [7:0] out0,
  output [7:0] out8,
  output [7:0] out1,
  output [7:0] out9,
  output [7:0] out2,
  output [7:0] out10,
  output [7:0] out3,
  output [7:0] out11,
  output [7:0] out4,
  output [7:0] out12,
  output [7:0] out5,
  output [7:0] out13,
  output [7:0] out6,
  output [7:0] out14,
  output [7:0] out7,
  output [7:0] out15
);

  assign out0 = in0 ^ kin0;  // XOR_Gate xor_1, 8 bits wide
  assign out1 = in1 ^ kin1;  // XOR_Gate xor_2, 8 bits wide
  assign out2 = in2 ^ kin2;  // XOR_Gate xor_3, 8 bits wide
  assign out3 = in3 ^ kin3;  // XOR_Gate xor_4, 8 bits wide
  assign out4 = in4 ^ kin4;  // XOR_Gate xor_5, 8 bits wide
  assign out5 = in5 ^ kin5;  // XOR_Gate xor_6, 8 bits wide
  assign out6 = in6 ^ kin6;  // XOR_Gate xor_7, 8 bits wide
  assign out7 = in7 ^ kin7;  // XOR_Gate xor_8, 8 bits wide
  assign out8 = in8 ^ kin8;  // XOR_Gate xor_9, 8 bits wide
  assign out9 = in9 ^ kin9;  // XOR_Gate xor_10, 8 bits wide
  assign out10 = in10 ^ kin10;  // XOR_Gate xor_11, 8 bits wide
  assign out11 = in11 ^ kin11;  // XOR_Gate xor_12, 8 bits wide
  assign out12 = in12 ^ kin12;  // XOR_Gate xor_13, 8 bits wide
  assign out13 = in13 ^ kin13;  // XOR_Gate xor_14, 8 bits wide
  assign out14 = in14 ^ kin14;  // XOR_Gate xor_15, 8 bits wide
  assign out15 = in15 ^ kin15;  // XOR_Gate xor_16, 8 bits wide
endmodule

module byte_substitute (
  input  [7:0] in0,
  input  [7:0] in1,
  input  [7:0] in2,
  input  [7:0] in3,
  input  [7:0] in4,
  input  [7:0] in5,
  input  [7:0] in6,
  input  [7:0] in7,
  input  [7:0] in8,
  input  [7:0] in9,
  input  [7:0] in10,
  input  [7:0] in11,
  input  [7:0] in12,
  input  [7:0] in13,
  input  [7:0] in14,
  input  [7:0] in15,
  output [7:0] out0,
  output [7:0] out1,
  output [7:0] out2,
  output [7:0] out3,
  output [7:0] out4,
  output [7:0] out5,
  output [7:0] out6,
  output [7:0] out7,
  output [7:0] out8,
  output [7:0] out9,
  output [7:0] out10,
  output [7:0] out11,
  output [7:0] out12,
  output [7:0] out13,
  output [7:0] out14,
  output [7:0] out15
);

  s_box s_box_1 (.in(in0), .out(out0));
  s_box s_box_2 (.in(in1), .out(out1));
  s_box s_box_3 (.in(in2), .out(out2));
  s_box s_box_4 (.in(in3), .out(out3));
  s_box s_box_5 (.in(in4), .out(out4));
  s_box s_box_6 (.in(in5), .out(out5));
  s_box s_box_7 (.in(in6), .out(out6));
  s_box s_box_8 (.in(in7), .out(out7));
  s_box s_box_9 (.in(in8), .out(out8));
  s_box s_box_10 (.in(in9), .out(out9));
  s_box s_box_11 (.in(in10), .out(out10));
  s_box s_box_12 (.in(in11), .out(out11));
  s_box s_box_13 (.in(in12), .out(out12));
  s_box s_box_14 (.in(in13), .out(out13));
  s_box s_box_15 (.in(in14), .out(out14));
  s_box s_box_16 (.in(in15), .out(out15));
endmodule

module raw_shift (
  input  [7:0] in0,
  input  [7:0] in4,
  input  [7:0] in8,
  input  [7:0] in12,
  input  [7:0] in1,
  input  [7:0] in5,
  input  [7:0] in9,
  input  [7:0] in13,
  input  [7:0] in2,
  input  [7:0] in6,
  input  [7:0] in10,
  input  [7:0] in14,
  input  [7:0] in3,
  input  [7:0] in7,
  input  [7:0] in11,
  input  [7:0] in15,
  output [7:0] out0,
  output [7:0] out4,
  output [7:0] out8,
  output [7:0] out12,
  output [7:0] out1,
  output [7:0] out5,
  output [7:0] out9,
  output [7:0] out13,
  output [7:0] out2,
  output [7:0] out6,
  output [7:0] out10,
  output [7:0] out14,
  output [7:0] out3,
  output [7:0] out7,
  output [7:0] out11,
  output [7:0] out15
);


  assign out0 = in0;
  assign out1 = in5;
  assign out2 = in10;
  assign out3 = in15;
  assign out4 = in4;
  assign out5 = in9;
  assign out6 = in14;
  assign out7 = in3;
  assign out8 = in8;
  assign out9 = in13;
  assign out10 = in2;
  assign out11 = in7;
  assign out12 = in12;
  assign out13 = in1;
  assign out14 = in6;
  assign out15 = in11;
endmodule

module column_mix (
  input  [7:0] in0,
  input  [7:0] in1,
  input  [7:0] in2,
  input  [7:0] in3,
  input  [7:0] in4,
  input  [7:0] in5,
  input  [7:0] in6,
  input  [7:0] in7,
  input  [7:0] in8,
  input  [7:0] in9,
  input  [7:0] in10,
  input  [7:0] in11,
  input  [7:0] in12,
  input  [7:0] in13,
  input  [7:0] in14,
  input  [7:0] in15,
  output [7:0] out0,
  output [7:0] out1,
  output [7:0] out2,
  output [7:0] out3,
  output [7:0] out4,
  output [7:0] out5,
  output [7:0] out6,
  output [7:0] out7,
  output [7:0] out8,
  output [7:0] out9,
  output [7:0] out10,
  output [7:0] out11,
  output [7:0] out12,
  output [7:0] out13,
  output [7:0] out14,
  output [7:0] out15
);

  column_mix_col column_mix_col_1 (
    .in0(in0), .in1(in1), .in2(in2), .in3(in3), .out0(out0), .out1(out1), .out2(out2), .out3(out3));
  column_mix_col column_mix_col_2 (
    .in0(in4), .in1(in5), .in2(in6), .in3(in7), .out0(out4), .out1(out5), .out2(out6), .out3(out7));
  column_mix_col column_mix_col_3 (
    .in0(in8), .in1(in9), .in2(in10), .in3(in11), .out0(out8), .out1(out9), .out2(out10), .out3(out11));
  column_mix_col column_mix_col_4 (
    .in0(in12), .in1(in13), .in2(in14), .in3(in15), .out0(out12), .out1(out13), .out2(out14), .out3(out15));
endmodule

module register256 (
  input  [7:0] in0,
  input  [7:0] in8,
  input  [7:0] in1,
  input  [7:0] in9,
  input  [7:0] in2,
  input  [7:0] in10,
  input  [7:0] in3,
  input  [7:0] in11,
  input  [7:0] in4,
  input  [7:0] in12,
  input  [7:0] in5,
  input  [7:0] in13,
  input  [7:0] in6,
  input  [7:0] in14,
  input  [7:0] in7,
  input  [7:0] in15,
  input  [7:0] kin0,
  input  [7:0] kin8,
  input  [7:0] kin1,
  input  [7:0] kin9,
  input  [7:0] kin2,
  input  [7:0] kin10,
  input  [7:0] kin3,
  input  [7:0] kin11,
  input  [7:0] kin4,
  input  [7:0] kin12,
  input  [7:0] kin5,
  input  [7:0] kin13,
  input  [7:0] kin6,
  input  [7:0] kin14,
  input  [7:0] kin7,
  input  [7:0] kin15,
  input  clk,
  output [7:0] out0,
  output [7:0] out8,
  output [7:0] out1,
  output [7:0] out9,
  output [7:0] out2,
  output [7:0] out10,
  output [7:0] out3,
  output [7:0] out11,
  output [7:0] out4,
  output [7:0] out12,
  output [7:0] out5,
  output [7:0] out13,
  output [7:0] out6,
  output [7:0] out14,
  output [7:0] out7,
  output [7:0] out15,
  output [7:0] kout0,
  output [7:0] kout8,
  output [7:0] kout1,
  output [7:0] kout9,
  output [7:0] kout2,
  output [7:0] kout10,
  output [7:0] kout3,
  output [7:0] kout11,
  output [7:0] kout4,
  output [7:0] kout12,
  output [7:0] kout5,
  output [7:0] kout13,
  output [7:0] kout6,
  output [7:0] kout14,
  output [7:0] kout7,
  output [7:0] kout15
);

  Register register_1 (.D(in0), .Q(out0), .clk(clk));  // open: en, clr
  Register register_2 (.D(in1), .Q(out1), .clk(clk));  // open: en, clr
  Register register_3 (.D(in2), .Q(out2), .clk(clk));  // open: en, clr
  Register register_4 (.D(in3), .Q(out3), .clk(clk));  // open: en, clr
  Register register_5 (.D(in4), .Q(out4), .clk(clk));  // open: en, clr
  Register register_6 (.D(in5), .Q(out5), .clk(clk));  // open: en, clr
  Register register_7 (.D(in6), .Q(out6), .clk(clk));  // open: en, clr
  Register register_8 (.D(in7), .Q(out7), .clk(clk));  // open: en, clr
  Register register_9 (.D(kin0), .Q(kout0), .clk(clk));  // open: en, clr
  Register register_10 (.D(kin1), .Q(kout1), .clk(clk));  // open: en, clr
  Register register_11 (.D(kin2), .Q(kout2), .clk(clk));  // open: en, clr
  Register register_12 (.D(kin3), .Q(kout3), .clk(clk));  // open: en, clr
  Register register_13 (.D(kin4), .Q(kout4), .clk(clk));  // open: en, clr
  Register register_14 (.D(kin5), .Q(kout5), .clk(clk));  // open: en, clr
  Register register_15 (.D(kin6), .Q(kout6), .clk(clk));  // open: en, clr
  Register register_16 (.D(kin7), .Q(kout7), .clk(clk));  // open: en, clr
  Register register_17 (.D(in8), .Q(out8), .clk(clk));  // open: en, clr
  Register register_18 (.D(in9), .Q(out9), .clk(clk));  // open: en, clr
  Register register_19 (.D(in10), .Q(out10), .clk(clk));  // open: en, clr
  Register register_20 (.D(in11), .Q(out11), .clk(clk));  // open: en, clr
  Register register_21 (.D(in12), .Q(out12), .clk(clk));  // open: en, clr
  Register register_22 (.D(in13), .Q(out13), .clk(clk));  // open: en, clr
  Register register_23 (.D(in14), .Q(out14), .clk(clk));  // open: en, clr
  Register register_24 (.D(in15), .Q(out15), .clk(clk));  // open: en, clr
  Register register_25 (.D(kin8), .Q(kout8), .clk(clk));  // open: en, clr
  Register register_26 (.D(kin9), .Q(kout9), .clk(clk));  // open: en, clr
  Register register_27 (.D(kin10), .Q(kout10), .clk(clk));  // open: en, clr
  Register register_28 (.D(kin11), .Q(kout11), .clk(clk));  // open: en, clr
  Register register_29 (.D(kin12), .Q(kout12), .clk(clk));  // open: en, clr
  Register register_30 (.D(kin13), .Q(kout13), .clk(clk));  // open: en, clr
  Register register_31 (.D(kin14), .Q(kout14), .clk(clk));  // open: en, clr
  Register register_32 (.D(kin15), .Q(kout15), .clk(clk));  // open: en, clr
endmodule

// cm_col
module column_mix_col (
  input  [7:0] in0,
  input  [7:0] in1,
  input  [7:0] in2,
  input  [7:0] in3,
  output [7:0] out0,
  output [7:0] out1,
  output [7:0] out2,
  output [7:0] out3
);

  column_mix_elm column_mix_elm_1 (.in0(in0), .in1(in1), .in2(in2), .in3(in3), .out(out0));
  column_mix_elm column_mix_elm_2 (.in0(in1), .in1(in2), .in2(in3), .in3(in0), .out(out1));
  column_mix_elm column_mix_elm_3 (.in0(in2), .in1(in3), .in2(in0), .in3(in1), .out(out2));
  column_mix_elm column_mix_elm_4 (.in0(in3), .in1(in0), .in2(in1), .in3(in2), .out(out3));
endmodule

// cm_elm
module column_mix_elm (
  input  [7:0] in0,
  input  [7:0] in1,
  input  [7:0] in2,
  input  [7:0] in3,
  output [7:0] out
);

  wire [7:0] column_mix_mul0x2_1_out, column_mix_mul0x2_2_out, xor_1_out, xor_2_out, xor_3_out;

  column_mix_mul0x2 column_mix_mul0x2_1 (.in(in0), .out(column_mix_mul0x2_1_out));
  column_mix_mul0x2 column_mix_mul0x2_2 (.in(in1), .out(column_mix_mul0x2_2_out));
  assign xor_1_out = in1 ^ column_mix_mul0x2_2_out;  // XOR_Gate xor_1, 8 bits wide
  assign xor_2_out = column_mix_mul0x2_1_out ^ xor_1_out;  // XOR_Gate xor_2, 8 bits wide
  assign xor_3_out = in2 ^ in3;  // XOR_Gate xor_3, 8 bits wide
  assign out = xor_2_out ^ xor_3_out;  // XOR_Gate xor_4, 8 bits wide
endmodule

// cm_mul0x2
module column_mix_mul0x2 (
  input  [7:0] in,
  output [7:0] out
);

  wire [7:0] xor_1_out;

  assign xor_1_out = 8'h1b ^ {in[6:0], 1'b0};  // XOR_Gate xor_1, 8 bits wide
  Multiplexer #(.width(8), .enable("false")) multiplexer_1 (
    .in0({in[6:0], 1'b0}), .in1(xor_1_out), .out(out), .sel(in[7]));
endmodule

// g
module key_gen_g (
  input  [31:0] in,
  input  [3:0] turn_number,
  output [31:0] out
);

  wire [7:0] rom_1_data, s_box_1_out;

  s_box s_box_1 (.in(in[23:16]), .out(s_box_1_out));
  s_box s_box_2 (.in(in[15:8]), .out(out[23:16]));
  s_box s_box_3 (.in(in[7:0]), .out(out[15:8]));
  s_box s_box_4 (.in(in[31:24]), .out(out[7:0]));
  ROM #(.addrWidth(4)) rom_1 (.addr(turn_number), .data(rom_1_data));  // open: sel
  assign out[31:24] = rom_1_data ^ s_box_1_out;  // XOR_Gate xor_1, 8 bits wide

  // Notes on the sheet:
  //   contents of rom_1 (hex, n*v repeats v):
  //   1 2 4 8 10 20 40 80 1b 36
endmodule

module s_box (
  input  [7:0] in,
  output [7:0] out
);

  ROM rom_1 (.addr(in), .data(out));  // open: sel

  // Notes on the sheet:
  //   contents of rom_1 (hex, n*v repeats v):
  //   63 7c 77 7b f2 6b 6f c5 30 1 67 2b fe d7 ab 76 ca 82 c9 7d fa 59 47 f0 ad d4 a2 af 9c a4 72 c0 b7 fd
  //   93 26 36 3f f7 cc 34 a5 e5 f1 71 d8 31 15 4 c7 23 c3 18 96 5 9a 7 12 80 e2 eb 27 b2 75 9 83 2c 1a 1b
  //   6e 5a a0 52 3b d6 b3 29 e3 2f 84 53 d1 0 ed 20 fc b1 5b 6a cb be 39 4a 4c 58 cf d0 ef aa fb 43 4d 33
  //   85 45 f9 2 7f 50 3c 9f a8 51 a3 40 8f 92 9d 38 f5 bc b6 da 21 10 ff f3 d2 cd c 13 ec 5f 97 44 17 c4
  //   a7 7e 3d 64 5d 19 73 60 81 4f dc 22 2a 90 88 46 ee b8 14 de 5e b db e0 32 3a a 49 6 24 5c c2 d3 ac
  //   62 91 95 e4 79 e7 c8 37 6d 8d d5 4e a9 6c 56 f4 ea 65 7a ae 8 ba 78 25 2e 1c a6 b4 c6 e8 dd 74 1f 4b
  //   bd 8b 8a 70 3e b5 66 48 3 f6 e 61 35 57 b9 86 c1 1d 9e e1 f8 98 11 69 d9 8e 94 9b 1e 87 e9 ce 55 28
  //   df 8c a1 89 d bf e6 42 68 41 99 2d f b0 54 bb 16
endmodule

module test_key_gen (
);

  wire key_gen_oneturn_1_p18, key_gen_oneturn_1_p19, key_gen_oneturn_1_p20, key_gen_oneturn_1_p21,
       key_gen_oneturn_1_p22, key_gen_oneturn_1_p23, key_gen_oneturn_1_p24, key_gen_oneturn_1_p25,
       key_gen_oneturn_1_p26, key_gen_oneturn_1_p27, key_gen_oneturn_1_p28, key_gen_oneturn_1_p29,
       key_gen_oneturn_1_p30, key_gen_oneturn_1_p31, key_gen_oneturn_1_p32, key_gen_oneturn_1_p33;

  // key_gen_oneturn key_gen_oneturn_1: pin names not known; wires that end beside it: 8'hf, 8'h15, 8'h71, 8'hc9, 8'h47, 8'hd9, 8'he8, 8'h59, 8'hc, 8'hb7, 8'had, 8'hd6, 8'haf, 8'h7f, 8'h67, 8'h98, 4'b0000, key_gen_oneturn_1_p18, key_gen_oneturn_1_p19, key_gen_oneturn_1_p20, key_gen_oneturn_1_p21, key_gen_oneturn_1_p22, key_gen_oneturn_1_p23, key_gen_oneturn_1_p24, key_gen_oneturn_1_p25, key_gen_oneturn_1_p26, key_gen_oneturn_1_p27, key_gen_oneturn_1_p28, key_gen_oneturn_1_p29, key_gen_oneturn_1_p30, key_gen_oneturn_1_p31, key_gen_oneturn_1_p32, key_gen_oneturn_1_p33
  // Probe on key_gen_oneturn_1_p18
  // Probe on key_gen_oneturn_1_p19
  // Probe on key_gen_oneturn_1_p20
  // Probe on key_gen_oneturn_1_p21
  // Probe on key_gen_oneturn_1_p22
  // Probe on key_gen_oneturn_1_p23
  // Probe on key_gen_oneturn_1_p24
  // Probe on key_gen_oneturn_1_p25
  // Probe on key_gen_oneturn_1_p26
  // Probe on key_gen_oneturn_1_p27
  // Probe on key_gen_oneturn_1_p28
  // Probe on key_gen_oneturn_1_p29
  // Probe on key_gen_oneturn_1_p30
  // Probe on key_gen_oneturn_1_p31
  // Probe on key_gen_oneturn_1_p32
  // Probe on key_gen_oneturn_1_p33
endmodule

module test_aes (
);

  wire clock_1_out;
  wire [31:0] aes_1_c0, aes_1_c1, aes_1_c2, aes_1_c3;

  aes aes_1 (
    .m0(32'h1234567), .m1(32'h89abcdef), .m2(32'hfedcba98), .m3(32'h76543210), .k0(32'hf1571c9),
    .k1(32'h47d9e859), .k2(32'hcb7add6), .k3(32'haf7f6798), .clk(clock_1_out), .c0(aes_1_c0), .c1(aes_1_c1),
    .c2(aes_1_c2), .c3(aes_1_c3));
  Clock clock_1 (.out(clock_1_out));
  RAM #(.addrWidth(2), .dataWidth(32), .bus("separate")) ram_1 (
    .addr(2'b00), .din(aes_1_c0), .clk(clock_1_out));  // open: data, str, sel, ld, clr
  RAM #(.addrWidth(2), .dataWidth(32), .bus("separate")) ram_2 (
    .addr(2'b00), .din(aes_1_c1), .clk(clock_1_out));  // open: data, str, sel, ld, clr
  RAM #(.addrWidth(2), .dataWidth(32), .bus("separate")) ram_3 (
    .addr(2'b00), .din(aes_1_c2), .clk(clock_1_out));  // open: data, str, sel, ld, clr
  RAM #(.addrWidth(2), .dataWidth(32), .bus("separate")) ram_4 (
    .addr(2'b00), .din(aes_1_c3), .clk(clock_1_out));  // open: data, str, sel, ld, clr

  // Notes on the sheet:
  //   m0
  //   m1
  //   m2
  //   m3
  //   k0
  //   k1
  //   k2
  //   k3
endmodule

module test_pipeline_aes (
  input  in_1
);

  wire clock_1_out;
  wire [7:0] counter_1_q;
  wire [31:0] aes_1_c0, aes_1_c1, aes_1_c2, aes_1_c3, rom_1_data, rom_2_data, rom_3_data, rom_4_data,
       rom_5_data, rom_6_data, rom_7_data, rom_8_data;

  Clock clock_1 (.out(clock_1_out));
  Counter counter_1 (.Q(counter_1_q), .clk(clock_1_out), .clr(in_1));  // open: load, D, count, carry
  ROM #(.dataWidth(32)) rom_1 (.addr(counter_1_q), .data(rom_1_data));  // open: sel
  ROM #(.dataWidth(32)) rom_2 (.addr(counter_1_q), .data(rom_2_data));  // open: sel
  ROM #(.dataWidth(32)) rom_3 (.addr(counter_1_q), .data(rom_3_data));  // open: sel
  ROM #(.dataWidth(32)) rom_4 (.addr(counter_1_q), .data(rom_4_data));  // open: sel
  ROM #(.dataWidth(32)) rom_5 (.addr(counter_1_q), .data(rom_5_data));  // open: sel
  ROM #(.dataWidth(32)) rom_6 (.addr(counter_1_q), .data(rom_6_data));  // open: sel
  ROM #(.dataWidth(32)) rom_7 (.addr(counter_1_q), .data(rom_7_data));  // open: sel
  ROM #(.dataWidth(32)) rom_8 (.addr(counter_1_q), .data(rom_8_data));  // open: sel
  aes aes_1 (
    .m0(rom_1_data), .m1(rom_2_data), .m2(rom_3_data), .m3(rom_4_data), .k0(rom_5_data), .k1(rom_6_data),
    .k2(rom_7_data), .k3(rom_8_data), .clk(clock_1_out), .c0(aes_1_c0), .c1(aes_1_c1), .c2(aes_1_c2),
    .c3(aes_1_c3));
  RAM #(.dataWidth(32), .bus("separate")) ram_1 (
    .addr(counter_1_q), .din(aes_1_c0), .clk(clock_1_out), .clr(in_1));  // open: data, str, sel, ld
  RAM #(.dataWidth(32), .bus("separate")) ram_2 (
    .addr(counter_1_q), .din(aes_1_c1), .clk(clock_1_out), .clr(in_1));  // open: data, str, sel, ld
  RAM #(.dataWidth(32), .bus("separate")) ram_3 (
    .addr(counter_1_q), .din(aes_1_c2), .clk(clock_1_out), .clr(in_1));  // open: data, str, sel, ld
  RAM #(.dataWidth(32), .bus("separate")) ram_4 (
    .addr(counter_1_q), .din(aes_1_c3), .clk(clock_1_out), .clr(in_1));  // open: data, str, sel, ld

  // Notes on the sheet:
  //   contents of rom_1 (hex, n*v repeats v):
  //   1234567 aaaaaaaa
  //   contents of rom_2 (hex, n*v repeats v):
  //   89abcdef bbbbbbbb
  //   contents of rom_3 (hex, n*v repeats v):
  //   fedcba98 cccccccc
  //   contents of rom_4 (hex, n*v repeats v):
  //   76543210 dddddddd
  //   contents of rom_5 (hex, n*v repeats v):
  //   f1571c9 deadbeef
  //   contents of rom_6 (hex, n*v repeats v):
  //   47d9e859 deadbeef
  //   contents of rom_7 (hex, n*v repeats v):
  //   cb7add6 deadbeef
  //   contents of rom_8 (hex, n*v repeats v):
  //   af7f6798 deadbeef
endmodule
